// Logisim project Memory_System.circ as structural Verilog
module Memory_Controller (
  input  Addr,
  input  Data_In,
  input  Data_Out,
  input  Clk,
  input  RST
);
endmodule

module Memory_Arbitter_MMIO (
  input  [31:0] in_1
);

  Register #(.width(32)) register_1 (.D(in_1));  // open: en, clk, Q, clr
endmodule
