// Logisim project CPU.circ as structural Verilog: 2 circuits, main circuit Die
module Die (
  input  [63:0] Data_In,
  input  RAM_Ready,
  input  [31:0] Addr_From_Perif_1,
  input  [31:0] Data_From_Perif_1,
  input  En_Write_1,
  input  DMA_REQ_1,
  input  [31:0] Addr_From_Perif_2,
  input  [31:0] Data_From_Perif_2,
  input  En_Write_2,
  input  DMA_REQ_2,
  input  [31:0] Addr_From_Perif_3,
  input  [31:0] Data_From_Perif_3,
  input  En_Write_3,
  input  DMA_REQ_3,
  input  Clk,
  input  RST,
  input  [63:0] ROM_Data_In,
  output [7:0] Write_Flags,
  output [31:0] Addr,
  output [31:0] Data_Out,
  output RST_Out,
  output Clk_Out,
  output Read_En,
  output Write_En,
  output [31:0] Addr_To_Perif_1,
  output [31:0] Data_To_Perif_1,
  output En_Read_To_Perif_1,
  output DMA_ACK_1,
  output [31:0] Addr_To_Perif_2,
  output [31:0] Data_To_Perif_2,
  output En_Read_To_Perif_2,
  output DMA_ACK_2,
  output [31:0] Addr_To_Perif_3,
  output [31:0] Data_To_Perif_3,
  output En_Read_To_Perif_3,
  output DMA_ACK_3,
  output HLT,
  output [19:0] ROM_Addr
);

  wire core_1_en_read, core_1_en_write, core_1_mem_req, DMA_ACK, mapper_1_is_rom,
       memory_controller_1_cpu_ack, memory_controller_1_stall, root_complex_1_bus_req, root_complex_1_is_ram,
       root_complex_1_read_req, root_complex_1_write_req, router_1_en_read_root, router_1_read_cpu_out,
       router_1_write_cpu_out;
  wire [2:0] core_1_tipo;
  wire [31:0] core_1_addr, core_1_data_out, root_complex_1_addr_to_cpu, root_complex_1_data_out,
       router_1_addr_to_lapic, router_1_addr_to_ram, router_1_addr_to_rom_mapper, router_1_addr_to_root,
       router_1_data_to_ram, router_1_data_to_root;
  wire [63:0] mapper_1_data_out, memory_controller_1_data_out, router_1_data_to_cpu;

  Router router_1 (
    .Is_ROM(mapper_1_is_rom), .Is_RAM(root_complex_1_is_ram), .Read_CPU(core_1_en_read),
    .Write_CPU(core_1_en_write), .DMA_ACK(DMA_ACK), .Read_REQ(root_complex_1_read_req),
    .Write_REQ(root_complex_1_write_req), .Data_From_RAM(memory_controller_1_data_out),
    .Data_From_ROM(mapper_1_data_out), .Data_From_Root(root_complex_1_data_out), .Addr_From_CPU(core_1_addr),
    .Addr_From_Root(root_complex_1_addr_to_cpu), .Data_From_CPU(core_1_data_out),
    .Read_CPU_Out(router_1_read_cpu_out), .Write_CPU_Out(router_1_write_cpu_out),
    .Data_To_CPU(router_1_data_to_cpu), .Addr_To_LAPIC(router_1_addr_to_lapic),
    .Addr_To_Root(router_1_addr_to_root), .Addr_To_ROM_Mapper(router_1_addr_to_rom_mapper),
    .Addr_To_RAM(router_1_addr_to_ram), .Data_To_RAM(router_1_data_to_ram),
    .Data_To_Root(router_1_data_to_root), .En_Read_Root(router_1_en_read_root));
  Memory_Controller memory_controller_1 (
    .Write_REQ(router_1_write_cpu_out), .Read_REQ(router_1_read_cpu_out),
    .Read_REQ_Root(root_complex_1_read_req), .Write_REQ_Root(root_complex_1_write_req),
    .Root_REQ(root_complex_1_bus_req), .Addr(router_1_addr_to_ram), .Data_In(router_1_data_to_ram),
    .RAM_Ready(RAM_Ready), .Tipo(core_1_tipo), .CPU_REQ(core_1_mem_req), .Data_From_RAM(Data_In),
    .DMA_ACK(DMA_ACK), .Data_Out(memory_controller_1_data_out), .CPU_ACK(memory_controller_1_cpu_ack),
    .Stall(memory_controller_1_stall), .Addr_To_RAM(Addr), .Data_To_RAM(Data_Out), .Write_En(Write_En),
    .Read_En(Read_En), .Write_Flags(Write_Flags));
  Core core_1 (
    .Data_In(router_1_data_to_cpu), .RAM_Ready(memory_controller_1_cpu_ack),
    .Stall(memory_controller_1_stall), .DMA_ACK(DMA_ACK), .Clk(Clk), .RST(RST),
    .Addr_LAPIC(router_1_addr_to_lapic), .HLT(HLT), .Addr(core_1_addr), .Tipo(core_1_tipo),
    .En_Read(core_1_en_read), .En_Write(core_1_en_write), .MEM_REQ(core_1_mem_req), .Data_Out(core_1_data_out));
  Mapper mapper_1 (
    .Addr(router_1_addr_to_rom_mapper), .Data_in(ROM_Data_In), .Data_Out(mapper_1_data_out),
    .Is_ROM(mapper_1_is_rom), .ROM_Addr(ROM_Addr));
  Root_Complex root_complex_1 (
    .Addr_From_Perif_1(Data_To_Perif_1), .Data_From_Perif_1(Data_From_Perif_1), .En_Write_1(En_Write_1),
    .DMA_REQ_1(DMA_REQ_1), .Addr_From_Perif_2(Data_To_Perif_2), .Data_From_Perif_2(Data_From_Perif_2),
    .En_Write_2(En_Write_2), .DMA_REQ_2(DMA_REQ_2), .Addr_From_Perif_3(Data_To_Perif_3),
    .Data_From_Perif_3(Data_From_Perif_3), .En_Write_3(En_Write_3), .DMA_REQ_3(DMA_REQ_3),
    .Data_In(router_1_data_to_root), .Addr(router_1_addr_to_root), .RST(RST), .Clk(Clk),
    .En_Read(router_1_en_read_root), .RAM_ACK(DMA_ACK), .DMA_ACK_3(DMA_ACK_3),
    .Addr_To_Perif_1(Addr_From_Perif_1), .Data_To_Perif_1(Addr_To_Perif_1),
    .En_Read_To_Perif_1(En_Read_To_Perif_1), .DMA_ACK_1(DMA_ACK_1), .Addr_To_Perif_2(Addr_From_Perif_2),
    .Data_To_Perif_2(Addr_To_Perif_2), .En_Read_To_Perif_2(En_Read_To_Perif_2), .DMA_ACK_2(DMA_ACK_2),
    .Addr_To_Perif_3(Addr_From_Perif_3), .Data_To_Perif_3(Addr_To_Perif_3),
    .En_Read_To_Perif_3(En_Read_To_Perif_3), .Addr_To_CPU(root_complex_1_addr_to_cpu),
    .Data_Out(root_complex_1_data_out), .Is_RAM(root_complex_1_is_ram), .Write_REQ(root_complex_1_write_req),
    .Read_REQ(root_complex_1_read_req), .Bus_REQ(root_complex_1_bus_req));

  assign Clk_Out = Clk;
  assign RST_Out = RST;
endmodule

module Router (
  input  [63:0] Data_From_RAM,
  input  [63:0] Data_From_ROM,
  input  [31:0] Data_From_Root,
  input  [31:0] Addr_From_CPU,
  input  [31:0] Addr_From_Root,
  input  [31:0] Data_From_CPU,
  input  Is_ROM,
  input  Is_RAM,
  input  Read_CPU,
  input  Write_CPU,
  input  DMA_ACK,
  input  Read_REQ,
  input  Write_REQ,
  output [63:0] Data_To_CPU,
  output [31:0] Addr_To_LAPIC,
  output [31:0] Addr_To_Root,
  output [31:0] Addr_To_ROM_Mapper,
  output [31:0] Addr_To_RAM,
  output [31:0] Data_To_RAM,
  output [31:0] Data_To_Root,
  output En_Read_Root,
  output Read_CPU_Out,
  output Write_CPU_Out
);

  wire Addr_Sel, Data_To_RAM_Sel, Data_To_Root_Sel, Enable;
  wire [1:0] Data_To_CPU_Sel;
  wire [31:0] bit_extender_2_out;
  wire [63:0] bit_extender_1_out;

  PLA #(.in_width(7), .out_width(6), .\table ("1x100xx 101000 # ROM\n01100xx 100000 # RRAM\n01010xx 100000 # WRAM\n00100xx 110000 # RRoot\n00010xx 100001 # WRoot\nxxxx110 100101 # R->P\nxxxx101 100110 # P->R")) pla_1 (
    .in({Is_ROM, Is_RAM, Read_CPU, Write_CPU, DMA_ACK, Read_REQ, Write_REQ}),
    .out({Enable, Data_To_CPU_Sel, Addr_Sel, Data_To_RAM_Sel, Data_To_Root_Sel}));
  PLA #(.in_width(7), .out_width(1), .\table ("00100xx 1 # RRoot")) pla_2 (
    .in({Is_ROM, Is_RAM, Read_CPU, Write_CPU, DMA_ACK, Read_REQ, Write_REQ}), .out(En_Read_Root));
  and and_1 (Read_CPU_Out, Read_CPU, ~Is_ROM);  // AND_Gate
  and and_2 (Write_CPU_Out, Write_CPU, ~Is_ROM);  // AND_Gate
  assign bit_extender_1_out = {{32{1'b0}}, Data_From_Root};  // Bit_Extender bit_extender_1
  Bit_Extender #(.in_width(64), .out_width(32), .\type ("zero")) bit_extender_2 (
    .in(Data_From_RAM), .out(bit_extender_2_out));
  Multiplexer #(.enable("true"), .select(2), .width(64)) multiplexer_1 (
    .in0(Data_From_RAM), .in1(Data_From_ROM), .in2(bit_extender_1_out), .out(Data_To_CPU),
    .sel(Data_To_CPU_Sel), .en(Enable));  // open: in3
  Multiplexer #(.enable("true"), .width(32)) multiplexer_2 (
    .in0(Addr_From_CPU), .in1(Addr_From_Root), .out(Addr_To_RAM), .sel(Addr_Sel), .en(Enable));
  Multiplexer #(.enable("true"), .width(32)) multiplexer_3 (
    .in0(Data_From_CPU), .in1(Data_From_Root), .out(Data_To_RAM), .sel(Data_To_RAM_Sel), .en(Enable));
  Multiplexer #(.enable("true"), .width(32)) multiplexer_4 (
    .in0(Data_From_CPU), .in1(bit_extender_2_out), .out(Data_To_Root), .sel(Data_To_Root_Sel), .en(Enable));

  assign Addr_To_LAPIC = Addr_From_CPU;
  assign Addr_To_ROM_Mapper = Addr_From_CPU;
  assign Addr_To_Root = Addr_From_CPU;
endmodule
