// Logisim project Control_FLush.circ as structural Verilog: 7 circuits, main circuit PC
module PC (
  input  [31:0] Addr,
  input  No_Instr,
  input  Stall,
  input  Clk,
  input  RST,
  output [31:0] Sum,
  output [31:0] PC_Out
);

  wire or_1_out;
  wire [31:0] multiplexer_1_out;

  or or_1 (or_1_out, No_Instr, ~Stall);  // OR_Gate
  Multiplexer #(.width(32)) multiplexer_1 (.in0(Addr), .in1(32'hffffffe0), .out(multiplexer_1_out), .sel(RST));
  Register #(.width(32)) register_1 (.D(multiplexer_1_out), .en(or_1_out), .clk(Clk), .Q(PC_Out));  // open: clr
  Adder #(.width(32)) adder_1 (.a(32'h4), .b(PC_Out), .out(Sum));  // open: cin, cout
endmodule

module Bypass (
  input  No_Bypass,
  input  [3:0] REG_A,
  input  [3:0] REG_B,
  input  [3:0] W_From_MEM,
  input  [3:0] W_From_WB,
  input  Res_From_MEM,
  input  Res_From_WB_Reg,
  input  Res_From_WB_RegE,
  input  [31:0] Data_From_MEM,
  input  [31:0] Data_From_WB,
  input  Inmd,
  output A,
  output B,
  output [31:0] Data_For_A,
  output [31:0] Data_For_B
);

  wire and_1_out, and_2_out, and_3_out, and_4_out, and_6_out, comparator_1_eq, comparator_2_eq,
       comparator_3_eq, comparator_4_eq, or_1_out, or_2_out, or_3_out, or_4_out, or_5_out;

  or or_1 (or_1_out, Res_From_WB_Reg, Res_From_WB_RegE);
  Comparator #(.width(4)) comparator_1 (.a(REG_A), .b(W_From_MEM), .eq(comparator_1_eq));  // open: gt, lt
  Comparator #(.width(4)) comparator_2 (.a(REG_B), .b(W_From_MEM), .eq(comparator_2_eq));  // open: gt, lt
  Comparator #(.width(4)) comparator_3 (.a(REG_A), .b(W_From_WB), .eq(comparator_3_eq));  // open: gt, lt
  Comparator #(.width(4)) comparator_4 (.a(REG_B), .b(W_From_WB), .eq(comparator_4_eq));  // open: gt, lt
  and and_1 (and_1_out, comparator_1_eq, Res_From_MEM);
  and and_2 (and_2_out, comparator_2_eq, Res_From_MEM);
  and and_3 (and_3_out, comparator_3_eq, or_1_out);
  and and_4 (and_4_out, comparator_4_eq, or_1_out);
  or or_2 (or_2_out, ~and_3_out, and_1_out);  // OR_Gate
  or or_3 (or_3_out, ~and_4_out, and_2_out);  // OR_Gate
  Multiplexer #(.width(32)) multiplexer_1 (.in0(Data_From_WB), .in1(Data_From_MEM), .out(Data_For_A), .sel(or_2_out));
  Multiplexer #(.width(32)) multiplexer_2 (.in0(Data_From_WB), .in1(Data_From_MEM), .out(Data_For_B), .sel(or_3_out));
  or or_4 (or_4_out, and_1_out, and_3_out);
  or or_5 (or_5_out, and_2_out, and_4_out);
  and and_5 (A, or_4_out, ~No_Bypass);  // AND_Gate
  and and_6 (and_6_out, or_5_out, ~Inmd);  // AND_Gate
  and and_7 (B, and_6_out, ~No_Bypass);  // AND_Gate
endmodule

module Flush (
  input  Branch,
  input  Clk,
  input  RST,
  input  HLT,
  output Flush_Out
);

  wire d_ff_1_q, or_2_out;

  D_Flip_Flop d_ff_1 (.D(Branch), .clk(Clk), .Q(d_ff_1_q), .reset(Flush_Out));  // open: Qn, preset
  or or_1 (Flush_Out, d_ff_1_q, or_2_out);
  or or_2 (or_2_out, RST, HLT);
endmodule

module Dec (
  input  Kernel,
  input  [31:0] Instr,
  output [3:0] A,
  output [3:0] B,
  output [3:0] E,
  output [31:0] Error_Code,
  output [2:0] Tipo,
  output [15:0] Ctrl_Word,
  output [15:0] Inmd,
  output [3:0] W,
  output [31:0] Instr_Out
);

  wire or_1_out, or_2_out, pla_1_out, pla_2_out;
  wire [1:0] not_1_out, pla_4_out;
  wire [15:0] pla_3_out;
  wire [31:0] pull_resistor_1_node;

  Multiplexer #(.width(4)) multiplexer_1 (.in0(Instr[23:20]), .in1(4'b0010), .out(E), .sel(or_1_out));
  PLA #(.in_width(5), .out_width(1), .\table ("00000 1 # NOP\n00001 1 # HLT\n00010 1 # ADD\n00011 1 # SUB\n00100 1 # MUL\n00101 1 # DIV\n00110 1 # NOR\n00111 1 # AND\n01000 1 # XOR\n01001 1 # RSH\n01010 1 # LSH\n01011 1 # GOF\n01100 1 # LDI\n01101 1 # ADI\n01110 1 # JMP\n01111 1 # BRH\n10000 1 # CAL\n10001 1 # RET\n10010 1 # LOD\n10011 1 # STR\n10100 1 # CYE\n10101 1 # CYR\n10110 1 # SCL\n10111 1 # SRT")) pla_1 (
    .in(Instr[28:24]), .out(pla_1_out));
  PLA #(.in_width(5), .out_width(1), .\table ("00001 1 # HLT\n10100 1 # CYE\n10101 1 # CYR\n10111 1 # SRT")) pla_2 (
    .in(Instr[28:24]), .out(pla_2_out));
  or or_1 (or_1_out, pla_3_out[3], pla_3_out[9]);
  PLA #(.in_width(5), .out_width(16), .\table ("00000 0000000000000000 # NOP\n00001 0000010000000000 # HLT\n00010 0000100000000100 # ADD\n00011 0000100000000100 # SUB\n00100 0000100000000100 # MUL\n00101 0000100000000100 # DIV\n00110 0000100000000100 # NOR\n00111 0000100000000100 # AND\n01000 0000100000000100 # XOR\n01001 0000100000000100 # RSH\n01010 0000100000000100 # LSH\n01011 0000100000000001 # GOF\n01100 0000100000000010 # LDI\n01101 0000100000000110 # ADI\n01110 0000000000010000 # JMP\n01111 0000000000100000 # BRH\n10000 0101000110001000 # CAL\n10001 0010000100000000 # RET\n10010 0000100110000010 # LOD\n10011 0000100000000010 # STR\n10100 1000100000000000 # CYE\n10101 0010000000000000 # CYR\n10110 0000000001010000 # SCL\n10111 0000000001000000 # SRT")) pla_3 (
    .in(Instr[28:24]), .out(pla_3_out));
  PLA #(.in_width(5), .\table ("01011 10 # GOF\n01100 10 # LDI\n01101 10 # ADI\n10010 01 # LOD\n10100 01 # CYE\n10101 01 # CYR")) pla_4 (
    .in(Instr[28:24]), .out(pla_4_out));
  not not_1 (not_1_out[0], pla_1_out);
  and and_1 (not_1_out[1], ~Kernel, pla_2_out);  // AND_Gate
  or or_2 (or_2_out, not_1_out[1], not_1_out[0]);
  Multiplexer #(.width(16)) multiplexer_2 (.in0(pla_3_out), .in1(16'h50), .out(Ctrl_Word), .sel(or_2_out));
  Multiplexer #(.select(2), .width(4)) multiplexer_3 (
    .in0(Instr[15:12]), .in1(Instr[19:16]), .in2(Instr[23:20]), .out(W), .sel(pla_4_out));  // open: in3
  Pull_Resistor pull_resistor_1 (.node(pull_resistor_1_node));
  Multiplexer #(.select(2), .width(32)) multiplexer_4 (
    .in0(pull_resistor_1_node), .in1(32'h4), .in2(32'h3), .in3(pull_resistor_1_node), .out(Error_Code),
    .sel(not_1_out));

  assign A = Instr[23:20];
  assign B = Instr[19:16];
  assign Inmd = Instr[15:0];
  assign Instr_Out = Instr;
  assign Tipo = Instr[31:29];
endmodule

module Instr_Fecher (
  input  [31:0] PC,
  input  En_Write,
  input  Flush,
  input  Clk,
  input  [63:0] Data_In,
  output En_PC,
  output [31:0] PC_Required,
  output Need_Instr,
  output [31:0] Instr_Out
);

  wire and_1_out, and_2_out, and_3_out, and_4_out, and_5_out, counter_1_carry, counter_2_carry, not_1_out,
       or_2_out, or_3_out, s_r_ff_1_q, Valid_q;
  wire [1:0] counter_1_q;
  wire [3:0] counter_2_q;
  wire [31:0] bit_extender_1_out, shifter_1_out;
  wire [63:0] multiplexer_1_out, shift_register_1_p5, shift_register_1_p6, shift_register_1_p7,
       shift_register_1_p8, shift_register_1_p9, shift_register_1_p10, shift_register_1_p11,
       shift_register_1_p12;

  S_R_Flip_Flop #(.trigger("falling")) Valid (
    .S(En_Write), .clk(Clk), .R(Flush), .Q(Valid_q), .reset(or_2_out));  // open: Qn, preset
  or or_1 (En_PC, Valid_q, En_Write);
  and and_1 (and_1_out, s_r_ff_1_q, En_Write);
  and and_2 (and_2_out, Need_Instr, En_PC, En_Write);
  and and_3 (and_3_out, ~counter_2_q[0], ~counter_2_q[1], ~counter_2_q[2], ~counter_2_q[3], counter_2_carry);  // AND_Gate
  or or_2 (or_2_out, and_3_out, Flush);
  and and_4 (and_4_out, En_PC, En_Write);
  // Probe on counter_1_q
  Counter #(.max('h3), .width(2)) counter_1 (
    .count(and_1_out), .Q(counter_1_q), .carry(counter_1_carry), .clk(Clk), .clr(or_3_out));  // open: load, D, up
  or or_3 (or_3_out, Need_Instr, Flush);
  and and_5 (and_5_out, and_4_out, Need_Instr);
  Counter #(.max('hf), .width(4)) counter_2 (
    .count(En_PC), .Q(counter_2_q), .carry(counter_2_carry), .up(and_5_out), .clk(Clk), .clr(Flush));  // open: load, D
  // Shift_Register #(.width(64)) shift_register_1: pin names not known; wires that end beside it: Flush, and_2_out, Clk, Data_In, shift_register_1_p5, shift_register_1_p6, shift_register_1_p7, shift_register_1_p8, shift_register_1_p9, shift_register_1_p10, shift_register_1_p11, shift_register_1_p12
  assign bit_extender_1_out = {{28{1'b0}}, counter_2_q};  // Bit_Extender bit_extender_1
  S_R_Flip_Flop #(.trigger("falling")) s_r_ff_1 (
    .S(counter_2_carry), .clk(Clk), .R(counter_1_carry), .Q(s_r_ff_1_q), .Qn(Need_Instr), .reset(or_2_out));  // open: preset
  Shifter #(.width(32)) shifter_1 (.in(bit_extender_1_out), .\dist (5'b00010), .out(shifter_1_out));
  // Probe on counter_2_q
  Adder #(.width(32)) adder_1 (.a(PC), .b(shifter_1_out), .out(PC_Required));  // open: cin, cout
  Multiplexer #(.select(3), .width(64)) multiplexer_1 (
    .in0(shift_register_1_p5), .in1(shift_register_1_p6), .in2(shift_register_1_p7),
    .in3(shift_register_1_p8), .in4(shift_register_1_p9), .in5(shift_register_1_p10),
    .in6(shift_register_1_p11), .in7(shift_register_1_p12), .out(multiplexer_1_out), .sel(counter_2_q[3:1]));
  not not_1 (not_1_out, counter_2_q[0]);
  Multiplexer #(.width(32)) multiplexer_2 (
    .in0(multiplexer_1_out[31:0]), .in1(multiplexer_1_out[63:32]), .out(Instr_Out), .sel(not_1_out));
endmodule

module Exception_Generator (
  input  [31:0] Cause_INT,
  input  IRQ,
  input  [31:0] New_Cause,
  input  Clk,
  input  RST,
  input  SRT,
  input  SCL,
  output W_Cause,
  output [31:0] Cause_Out
);

  wire and_1_out, comparator_1_gt, demultiplexer_1_out0, demultiplexer_1_out1, or_1_out, or_2_out, t_ff_1_q;
  wire [31:0] multiplexer_1_out;

  Comparator #(.mode("unsigned"), .width(32)) comparator_1 (
    .a(New_Cause), .b({32{1'b0}}), .gt(comparator_1_gt));  // open: eq, lt
  Multiplexer #(.width(32)) multiplexer_1 (
    .in0(Cause_INT), .in1(New_Cause), .out(multiplexer_1_out), .sel(comparator_1_gt));
  or or_1 (or_1_out, IRQ, comparator_1_gt);
  Demultiplexer demultiplexer_1 (
    .out0(demultiplexer_1_out0), .out1(demultiplexer_1_out1), .in(or_1_out), .sel(t_ff_1_q));
  T_Flip_Flop t_ff_1 (.T(demultiplexer_1_out0), .clk(Clk), .Q(t_ff_1_q), .reset(or_2_out));  // open: Qn, preset
  or or_2 (or_2_out, RST, SRT);
  and and_1 (and_1_out, demultiplexer_1_out1, t_ff_1_q);
  Multiplexer #(.width(32)) multiplexer_2 (.in0(multiplexer_1_out), .in1(32'h5), .out(Cause_Out), .sel(and_1_out));
  or or_3 (W_Cause, or_1_out, SCL);
endmodule

module Pruebas (
  input  in_1,
  input  in_2
);

  wire instr_fecher_1_en_pc, instr_fecher_1_need_instr;
  wire [19:0] bit_extender_1_out;
  wire [31:0] instr_fecher_1_instr_out, instr_fecher_1_pc_required, pc_1_pc_out, pc_1_sum;
  wire [63:0] undriven;

  // Probe on instr_fecher_1_pc_required
  Instr_Fecher instr_fecher_1 (
    .En_Write(instr_fecher_1_need_instr), .Flush(in_1), .Clk(in_2), .PC(pc_1_pc_out), .Data_In(undriven),
    .En_PC(instr_fecher_1_en_pc), .PC_Required(instr_fecher_1_pc_required),
    .Need_Instr(instr_fecher_1_need_instr), .Instr_Out(instr_fecher_1_instr_out));
  PC pc_1 (
    .Addr(pc_1_sum), .No_Instr(instr_fecher_1_en_pc), .Clk(in_2), .RST(in_1), .Sum(pc_1_sum),
    .PC_Out(pc_1_pc_out));  // open: Stall
  // Probe on pc_1_pc_out
  Bit_Extender #(.in_width(32), .out_width(20), .\type ("zero")) bit_extender_1 (
    .in(instr_fecher_1_pc_required), .out(bit_extender_1_out));
  // ROM #(.addrWidth(20), .line("octo"), .misaligned("true")) rom_1: pin names not known; wires that end beside it: bit_extender_1_out
  // Probe on {instr_fecher_1_instr_out[7:0], instr_fecher_1_instr_out[15:8], instr_fecher_1_instr_out[23:16], instr_fecher_1_instr_out[31:24]}

  // Notes on the sheet:
  //   contents of rom_1 (hex, n*v repeats v):
  //   1 1048543*0 c f0 ff f0 c e0 0 10 a fe f0 0 c e0 0 0 2 fe f0 0 e f
endmodule
