// Logisim project LAPIC.circ as structural Verilog
module Local_APIC (
  input  DMA_ACK,
  input  [31:0] Addr_From_Perif,
  input  [31:0] Data_In,
  input  [31:0] Addr_From_CPU,
  input  [1:0] RoW,
  input  CLk,
  input  RST,
  output [63:0] Data_Out,
  output MMIO_LAPIC,
  output [31:0] Cause,
  output IRQ
);

  wire bit_extender_2_out, in_service_register_1_valid_isr, interrupt_request_register_1_valid,
       mmio_1_eio_out, task_priority_register_1_isr_write, task_priority_register_1_valid_out;
  wire [6:0] in_service_register_1_actual_isr, interrupt_request_register_1_irr_out,
       task_priority_register_1_new_isr;
  wire [31:0] mmio_1_apic_config_out, mmio_1_data_out, mmio_1_timmer_id, mmio_1_timmer_start, mmio_1_tpr_out;
  wire [63:0] local_timmer_1_lvt_1, local_timmer_1_lvt_2, mmio_1_irr_mmio_1, mmio_1_irr_mmio_2;

  Local_Timmer local_timmer_1 (
    .RST(RST), .Clk(CLk), .Timmer_Max(mmio_1_timmer_start), .Timmer_Config(mmio_1_timmer_id),
    .LVT_1(local_timmer_1_lvt_1), .LVT_2(local_timmer_1_lvt_2));
  assign Data_Out = {{32{1'b0}}, mmio_1_data_out};  // Bit_Extender bit_extender_1
  Interrupt_Request_Register interrupt_request_register_1 (
    .Clk(CLk), .LVT_1(local_timmer_1_lvt_1), .LVT_2(local_timmer_1_lvt_2), .MMIO_1(mmio_1_irr_mmio_1),
    .MMIO_2(mmio_1_irr_mmio_2), .RST(RST), .IRR_Out(interrupt_request_register_1_irr_out),
    .Valid(interrupt_request_register_1_valid));
  MMIO mmio_1 (
    .Addr_CPU(Addr_From_CPU), .Addr_Perif(Addr_From_Perif), .DMA_ACK(DMA_ACK), .RST(RST), .Clk(CLk),
    .Data_In(Data_In), .RoW(RoW), .Data_Out(mmio_1_data_out), .Timmer_Start(mmio_1_timmer_start),
    .APIC_Config_Out(mmio_1_apic_config_out), .TPR_Out(mmio_1_tpr_out), .EIO_Out(mmio_1_eio_out),
    .Timmer_ID(mmio_1_timmer_id), .IRR_MMIO_1(mmio_1_irr_mmio_1), .IRR_MMIO_2(mmio_1_irr_mmio_2),
    .MMIO_LAPIC(MMIO_LAPIC));
  Bit_Extender #(.in_width(32), .out_width(1), .\type ("zero")) bit_extender_2 (
    .in(mmio_1_apic_config_out), .out(bit_extender_2_out));
  Task_Priority_Register task_priority_register_1 (
    .RST(RST), .ISR(in_service_register_1_actual_isr), .MMIO_TPR_In(mmio_1_tpr_out),
    .Valid(interrupt_request_register_1_valid), .IRR_In(interrupt_request_register_1_irr_out), .Clk(CLk),
    .ISR_Write(task_priority_register_1_isr_write), .Valid_Out(task_priority_register_1_valid_out),
    .New_ISR(task_priority_register_1_new_isr));
  In_Service_Register in_service_register_1 (
    .RST(RST), .Clk(CLk), .ISR_Write(task_priority_register_1_isr_write),
    .New_ISR(task_priority_register_1_new_isr), .Valid(task_priority_register_1_valid_out),
    .EIO(mmio_1_eio_out), .Actual_ISR(in_service_register_1_actual_isr), .Cause(Cause),
    .Valid_ISR(in_service_register_1_valid_isr));
  and and_1 (IRQ, in_service_register_1_valid_isr, bit_extender_2_out);
endmodule

module In_Service_Register (
  input  EIO,
  input  RST,
  input  Clk,
  input  ISR_Write,
  input  [6:0] New_ISR,
  input  Valid,
  output [6:0] Actual_ISR,
  output [31:0] Cause,
  output Valid_ISR
);

  wire [31:0] bit_extender_1_out;
  wire [63:0] Actual_ISR_A, Actual_ISR_B, ISR_A_q, ISR_B_q, multiplexer_1_out, multiplexer_2_out, or_1_out,
       or_2_out, pri_decoder_1_a, pri_decoder_1_b;

  Pri_Decoder pri_decoder_1 (.INDEX(New_ISR), .VALID(Valid), .A(pri_decoder_1_a), .B(pri_decoder_1_b));
  assign or_1_out = ISR_A_q | pri_decoder_1_a;  // OR_Gate or_1, 64 bits wide
  assign or_2_out = ISR_B_q | pri_decoder_1_b;  // OR_Gate or_2, 64 bits wide
  Multiplexer #(.width(64)) multiplexer_1 (.in0(or_1_out), .in1(Actual_ISR_A), .out(multiplexer_1_out), .sel(EIO));
  Multiplexer #(.width(64)) multiplexer_2 (.in0(or_2_out), .in1(Actual_ISR_B), .out(multiplexer_2_out), .sel(EIO));
  Register #(.width(64)) ISR_A (.D(multiplexer_1_out), .en(ISR_Write), .clk(Clk), .Q(ISR_A_q), .clr(RST));
  Register #(.width(64)) ISR_B (.D(multiplexer_2_out), .en(ISR_Write), .clk(Clk), .Q(ISR_B_q), .clr(RST));
  Pri_Encoder pri_encoder_1 (.A(ISR_A_q), .B(ISR_B_q), .INDEX(Actual_ISR), .VALID(Valid_ISR));
  assign bit_extender_1_out = {{25{1'b0}}, Actual_ISR};  // Bit_Extender bit_extender_1
  Adder #(.width(32)) adder_1 (.a(32'h20), .b(bit_extender_1_out), .out(Cause));  // open: cin, cout
  Pri_Decoder pri_decoder_2 (.INDEX(Actual_ISR), .VALID(Valid_ISR), .A(Actual_ISR_A), .B(Actual_ISR_B));
endmodule

module Task_Priority_Register (
  input  Clk,
  input  RST,
  input  [6:0] ISR,
  input  [31:0] MMIO_TPR_In,
  input  Valid,
  input  [6:0] IRR_In,
  output ISR_Write,
  output Valid_Out,
  output [6:0] New_ISR
);

  wire comparator_1_gt, not_1_out;
  wire [6:0] bit_extender_1_out, multiplexer_1_out, TPR_q;

  Bit_Extender #(.in_width(32), .out_width(7), .\type ("zero")) bit_extender_1 (
    .in(MMIO_TPR_In), .out(bit_extender_1_out));
  Register #(.width(7)) TPR (.D(bit_extender_1_out), .clk(Clk), .Q(TPR_q), .clr(RST));  // open: en
  Comparator #(.mode("unsigned"), .width(7)) comparator_1 (.a(ISR), .b(TPR_q), .gt(comparator_1_gt));  // open: eq, lt
  Multiplexer #(.width(7)) multiplexer_1 (.in0(TPR_q), .in1(ISR), .out(multiplexer_1_out), .sel(comparator_1_gt));
  Comparator #(.mode("unsigned"), .width(7)) comparator_2 (
    .a(multiplexer_1_out), .b(IRR_In), .lt(ISR_Write));  // open: gt, eq
  not not_1 (not_1_out, ISR_Write);
  and and_1 (Valid_Out, ISR_Write, Valid);
  Multiplexer #(.enable("true"), .width(7)) multiplexer_2 (
    .in0(IRR_In), .in1({7{1'b0}}), .out(New_ISR), .sel(not_1_out), .en(Valid));
endmodule

module Interrupt_Request_Register (
  input  RST,
  input  Clk,
  input  [63:0] LVT_1,
  input  [63:0] LVT_2,
  input  [63:0] MMIO_1,
  input  [63:0] MMIO_2,
  output [6:0] IRR_Out,
  output Valid
);

  wire [63:0] IRR_A_q, IRR_B_q, or_1_out, or_2_out;

  assign or_1_out = IRR_A_q | LVT_1 | MMIO_1 | {64{1'b0}};  // OR_Gate or_1, 64 bits wide
  assign or_2_out = {64{1'b0}} | MMIO_2 | LVT_2 | IRR_B_q;  // OR_Gate or_2, 64 bits wide
  Register #(.width(64)) IRR_A (.D(or_1_out), .clk(Clk), .Q(IRR_A_q), .clr(RST));  // open: en
  Register #(.width(64)) IRR_B (.D(or_2_out), .clk(Clk), .Q(IRR_B_q), .clr(RST));  // open: en
  Pri_Encoder pri_encoder_1 (.A(IRR_A_q), .B(IRR_B_q), .INDEX(IRR_Out), .VALID(Valid));

  // Notes on the sheet:
  //   IPIs
endmodule

module MMIO (
  input  [31:0] Addr_CPU,
  input  [31:0] Addr_Perif,
  input  DMA_ACK,
  input  RST,
  input  Clk,
  input  [31:0] Data_In,
  input  [1:0] RoW,
  output MMIO_LAPIC,
  output [31:0] APIC_Config_Out,
  output [31:0] TPR_Out,
  output EIO_Out,
  output [31:0] Timmer_ID,
  output [31:0] Timmer_Start,
  output [63:0] IRR_MMIO_1,
  output [63:0] IRR_MMIO_2,
  output [31:0] Data_Out
);

  wire and_1_out, and_3_out, bit_extender_1_out, comparator_1_eq, d_ff_1_q, decoder_1_out0, decoder_1_out1,
       decoder_1_out2, decoder_1_out3, decoder_1_out4, decoder_1_out5, decoder_1_out6, MSI_Line_ACK, or_1_out;
  wire [3:0] Addr, bit_extender_4_out, demultiplexer_1_out1;
  wire [11:0] shifter_1_out;
  wire [31:0] Base_Addr_q, bit_extender_2_out, bit_extender_3_out, LAPIC_ID_q, multiplexer_1_out,
       multiplexer_2_out;

  Multiplexer #(.width(32)) multiplexer_1 (.in0(Addr_CPU), .in1(Addr_Perif), .out(multiplexer_1_out), .sel(DMA_ACK));
  or or_1 (or_1_out, RoW[0], DMA_ACK);
  and and_1 (and_1_out, MMIO_LAPIC, MSI_Line_ACK, or_1_out);
  Decoder #(.select(4)) decoder_1 (
    .out0(decoder_1_out0), .out1(decoder_1_out1), .out2(decoder_1_out2), .out3(decoder_1_out3),
    .out4(decoder_1_out4), .out5(decoder_1_out5), .out6(decoder_1_out6), .sel(Addr), .en(and_1_out));  // open: out7, out8, out9, out10, out11, out12, out13, out14, out15
  D_Flip_Flop d_ff_1 (.clk(Clk), .Q(d_ff_1_q), .preset(MMIO_LAPIC), .reset(RST));  // open: D, Qn
  Register #(.width(32)) Base_Addr (.D(Data_In), .en(decoder_1_out0), .Q(Base_Addr_q), .clk(Clk), .clr(RST));
  Register #(.width(32)) LAPIC_ID (.D(Data_In), .en(decoder_1_out1), .clk(Clk), .Q(LAPIC_ID_q), .clr(RST));
  Register #(.width(32)) APIC_Config (.D(Data_In), .en(decoder_1_out2), .clk(Clk), .Q(APIC_Config_Out), .clr(RST));
  Register #(.width(32)) TPR (.D(Data_In), .en(decoder_1_out3), .clk(Clk), .Q(TPR_Out), .clr(RST));
  Bit_Extender #(.in_width(32), .out_width(1)) bit_extender_1 (.in(Data_In), .out(bit_extender_1_out));
  Register #(.width(32)) Timmer (.D(Data_In), .en(decoder_1_out5), .clk(Clk), .Q(Timmer_ID), .clr(RST));
  Register #(.width(32)) Start_Timmer (.D(Data_In), .en(decoder_1_out6), .clk(Clk), .Q(Timmer_Start), .clr(RST));
  Multiplexer #(.width(32)) multiplexer_2 (
    .in0(32'hfee00000), .in1(Base_Addr_q), .out(multiplexer_2_out), .sel(d_ff_1_q));
  and and_2 (EIO_Out, bit_extender_1_out, decoder_1_out4);
  and and_3 (and_3_out, MMIO_LAPIC, ~DMA_ACK, ~RoW[0]);  // AND_Gate
  Shifter #(.shift("lr"), .width(12)) shifter_1 (.in(multiplexer_1_out[11:0]), .\dist (4'b0010), .out(shifter_1_out));
  assign bit_extender_2_out = {{12{1'b0}}, multiplexer_1_out[31:12]};  // Bit_Extender bit_extender_2
  assign bit_extender_3_out = {{12{1'b0}}, multiplexer_2_out[31:12]};  // Bit_Extender bit_extender_3
  Multiplexer #(.enable("true"), .select(4), .width(32)) multiplexer_3 (
    .in0(multiplexer_2_out), .in1(LAPIC_ID_q), .in2(APIC_Config_Out), .in3(TPR_Out), .in5(Timmer_ID),
    .in6(Timmer_Start), .out(Data_Out), .sel(Addr), .en(and_3_out));  // open: in4, in7, in8, in9, in10, in11, in12, in13, in14, in15
  Bit_Extender #(.in_width(12), .out_width(4), .\type ("zero")) bit_extender_4 (
    .in(shifter_1_out), .out(bit_extender_4_out));
  Demultiplexer #(.enable("true"), .width(4)) demultiplexer_1 (
    .out0(Addr), .out1(demultiplexer_1_out1), .in(bit_extender_4_out), .sel(DMA_ACK), .en(MMIO_LAPIC));
  Comparator #(.mode("unsigned"), .width(32)) comparator_1 (
    .a(bit_extender_2_out), .b(bit_extender_3_out), .eq(comparator_1_eq));  // open: gt, lt
  PLA #(.in_width(4), .out_width(1), .\table ("0111 1 # 7\n1000 1 # 8\n1001 1 # 9\n1010 1 # 10")) pla_1 (
    .in(demultiplexer_1_out1), .out(MSI_Line_ACK));
  and and_4 (MMIO_LAPIC, comparator_1_eq, RoW[1]);

  assign IRR_MMIO_1 = {Data_In, Data_In};
  assign IRR_MMIO_2 = {Data_In, Data_In};

  // Other names for the same wires on the sheet: Enable = MMIO_LAPIC; RAM = RoW[1]

  // Notes on the sheet:
  //   Atributes
  //   Config
  //   LVTs
  //   Timer
  //   MSI_MMIO
endmodule

module Local_Timmer (
  input  [31:0] Timmer_Config,
  input  RST,
  input  Clk,
  input  [31:0] Timmer_Max,
  output [63:0] LVT_1,
  output [63:0] LVT_2
);

  wire and_1_out, bit_extender_1_out, counter_1_carry;

  Bit_Extender #(.in_width(25), .out_width(1), .\type ("zero")) bit_extender_1 (
    .in(Timmer_Config[31:7]), .out(bit_extender_1_out));
  Counter #(.max('hffffffff), .width(32)) counter_1 (
    .clr(RST), .load(counter_1_carry), .up(1'b0), .count(bit_extender_1_out), .clk(Clk), .D(Timmer_Max),
    .carry(counter_1_carry));  // open: Q
  and and_1 (and_1_out, bit_extender_1_out, counter_1_carry);
  Pri_Decoder pri_decoder_1 (.INDEX(Timmer_Config[6:0]), .VALID(and_1_out), .A(LVT_1), .B(LVT_2));
endmodule

// VHDL entity Pri_Encoder, as the project stores it:
-- =============================================================================
-- Priority Encoder - Codificador de Prioridad
-- =============================================================================
-- Descripcion:
--   Recibe dos operandos de 64 bits (A y B). Los concatena en un vector de
--   128 bits donde B ocupa los bits [127:64] y A los bits [63:0].
--   Devuelve de forma ASINCRONA (combinacional puro) un codigo de 7 bits que
--   representa la posicion del bit '1' mas significativo (MSB activo).
--
--   Si ningun bit esta activo, la salida es "0000000" y la senal VALID = '0'.
--
-- Entradas:
--   A       : std_logic_vector(63 downto 0)  -- Operando bajo  [63:0]
--   B       : std_logic_vector(63 downto 0)  -- Operando alto [127:64]
--
-- Salidas:
--   INDEX   : std_logic_vector(6 downto 0)   -- Posicion del bit mas alto activo
--   VALID   : std_logic                      -- '1' si al menos un bit esta activo
-- =============================================================================

library IEEE;
use IEEE.STD_LOGIC_1164.ALL;
use IEEE.NUMERIC_STD.ALL;

-- -----------------------------------------------------------------------------
-- Entity
-- -----------------------------------------------------------------------------
entity Pri_Encoder is
    port (
        -- Operandos de entrada (64 bits cada uno)
        A     : in  std_logic_vector(63 downto 0);   -- bits [63:0]
        B     : in  std_logic_vector(63 downto 0);   -- bits [127:64]

        -- Resultado combinacional
        INDEX : out std_logic_vector(6 downto 0);    -- posicion del MSB activo
        VALID : out std_logic                         -- indica al menos un bit activo
    );
end entity Pri_Encoder;

-- -----------------------------------------------------------------------------
-- Architecture - Combinacional / Asincrona
-- -----------------------------------------------------------------------------
architecture rtl of Pri_Encoder is

    -- Vector interno de 128 bits: B en la mitad alta, A en la baja
    signal combined : std_logic_vector(127 downto 0);

begin

    -- -------------------------------------------------------------------------
    -- Concatenacion: B es mas significativo que A
    -- combined[127:64] = B
    -- combined[ 63: 0] = A
    -- -------------------------------------------------------------------------
    combined <= B & A;

    -- -------------------------------------------------------------------------
    -- Proceso combinacional - Priority Encoder
    -- Recorre el vector desde el bit mas alto (127) hacia el mas bajo (0).
    -- En cuanto encuentra el primer '1', codifica su posicion en INDEX y
    -- activa VALID. Si no hay ningun '1', INDEX = 0 y VALID = '0'.
    -- -------------------------------------------------------------------------
    PRIORITY_ENC : process(combined)
        variable found : boolean;
    begin
        INDEX <= (others => '0');
        VALID <= '0';
        found := false;

        for i in 127 downto 0 loop
            if (combined(i) = '1') and (not found) then
                INDEX <= std_logic_vector(to_unsigned(i, 7));
                VALID <= '1';
                found := true;
            end if;
        end loop;

    end process PRIORITY_ENC;

end architecture rtl;

// VHDL entity Pri_Decoder, as the project stores it:
-- =============================================================================
-- Priority Decoder - Decodificador de Prioridad
-- =============================================================================
-- Descripcion:
--   Es el inverso del Pri_Encoder. Recibe un codigo de 7 bits (INDEX) que
--   representa una posicion de bit entre 0 y 127, y genera un vector de 128
--   bits "one-hot" (un solo bit activo) particionado en dos salidas de 64 bits.
--
--   La salida sigue el mismo convenio que Pri_Encoder:
--     A   cubre los bits  [63:  0]  (posiciones  0 ..  63)
--     B   cubre los bits [127: 64]  (posiciones 64 .. 127)
--
--   Si VALID = '0' ambas salidas son todo ceros, independientemente de INDEX.
--
-- Entradas:
--   INDEX  : std_logic_vector(6 downto 0)  -- Posicion del bit a activar (0-127)
--   VALID  : std_logic                     -- '1' habilita la decodificacion
--
-- Salidas:
--   A      : std_logic_vector(63 downto 0) -- bits [63:0]   del resultado
--   B      : std_logic_vector(63 downto 0) -- bits [127:64] del resultado
-- =============================================================================

library IEEE;
use IEEE.STD_LOGIC_1164.ALL;
use IEEE.NUMERIC_STD.ALL;

-- -----------------------------------------------------------------------------
-- Entity
-- -----------------------------------------------------------------------------
entity Pri_Decoder is
    port (
        -- Entrada codificada
        INDEX  : in  std_logic_vector(6 downto 0);   -- posicion del bit activo
        VALID  : in  std_logic;                       -- habilita la decodificacion

        -- Salidas one-hot (64 bits cada una)
        A      : out std_logic_vector(63 downto 0);   -- bits [63:0]
        B      : out std_logic_vector(63 downto 0)    -- bits [127:64]
    );
end entity Pri_Decoder;

-- -----------------------------------------------------------------------------
-- Architecture - Combinacional / Asincrona
-- -----------------------------------------------------------------------------
architecture rtl of Pri_Decoder is

    -- Vector interno de 128 bits (one-hot)
    signal combined : std_logic_vector(127 downto 0);

begin

    -- -------------------------------------------------------------------------
    -- Proceso combinacional - Priority Decoder
    -- Activa solo el bit cuya posicion coincide con INDEX.
    -- Si VALID = '0', el resultado es todo ceros.
    -- -------------------------------------------------------------------------
    PRIORITY_DEC : process(INDEX, VALID)
        variable pos : integer range 0 to 127;
    begin
        combined <= (others => '0');          -- default: todo apagado

        if VALID = '1' then
            pos := to_integer(unsigned(INDEX));
            combined(pos) <= '1';             -- activa el bit indicado
        end if;

    end process PRIORITY_DEC;

    -- -------------------------------------------------------------------------
    -- Separacion del vector en dos salidas de 64 bits
    -- B <-- combined[127:64]   (posiciones 64 .. 127)
    -- A <-- combined[ 63: 0]   (posiciones  0 ..  63)
    -- -------------------------------------------------------------------------
    A <= combined(63  downto  0);
    B <= combined(127 downto 64);

end architecture rtl;
