// Logisim project MEM_V2.circ as structural Verilog
module MMU (
  input  Clk,
  input  RST,
  input  IF_REQ,
  input  [31:0] IF_Addr,
  input  MEM_REQ,
  input  [31:0] MEM_Addr
);

  wire and_1_out, and_2_out, and_3_out, and_4_out, not_1_out, or_1_out, tlb_lru_1_hit, tlb_lru_2_hit,
       undriven, undriven_2, undriven_5;
  wire [31:0] undriven_3, undriven_4;

  not not_1 (not_1_out, MEM_REQ);
  or or_1 (or_1_out, MEM_REQ, IF_REQ);
  and and_1 (and_1_out, undriven, IF_REQ);
  and and_2 (and_2_out, undriven, undriven_2);
  // OR_Gate or_2 has open pins: in0=tlb_lru_1_hit, in1=tlb_lru_2_hit, out=open
  TLB_LRU tlb_lru_1 (
    .clk(Clk), .reset(RST), .lookup_en(and_1_out), .pcid(undriven_3), .virt_addr(IF_Addr),
    .write_en(and_2_out), .write_phys(undriven_4), .hit(tlb_lru_1_hit));  // open: phys_frame
  and and_3 (and_3_out, undriven, MEM_REQ);
  and and_4 (and_4_out, undriven, undriven_5);
  TLB_LRU tlb_lru_2 (
    .clk(Clk), .reset(RST), .lookup_en(and_3_out), .pcid(undriven_3), .virt_addr(MEM_Addr),
    .write_en(and_4_out), .write_phys(undriven_4), .hit(tlb_lru_2_hit));  // open: phys_frame
  Page_Walker page_walker_1 ();  // open: CR3, IF_REQ, REQ, MEM_Addr, IF_Addr, En_MMU, Hit, Data_In, d_TLB, i_TLB, Clk, RST, Stall_RAM, TLB_Write, Addr, Write_d_TLB, Write_i_TLB, IF_Write, STALL

  // Notes on the sheet:
  //   IF
  //   REQ
  //   Write
  //   En TLB
  //   Write Addr
  //   PCID
  //   V Addr
  //   No Hit
  //   Write
  //   V_Addr
endmodule

module Page_Walker (
  input  [31:0] CR3,
  input  IF_REQ,
  input  REQ,
  input  [31:0] MEM_Addr,
  input  [31:0] IF_Addr,
  input  En_MMU,
  input  Hit,
  input  [31:0] Data_In,
  input  [31:0] d_TLB,
  input  [31:0] i_TLB,
  input  Clk,
  input  RST,
  input  Stall_RAM,
  output [31:0] TLB_Write,
  output [31:0] Addr,
  output Write_d_TLB,
  output Write_i_TLB,
  output IF_Write,
  output STALL
);

  wire and_2_out, and_3_out, and_4_out, En_MMU_t;
  wire [1:0] multiplexer_6_out, Mux, Page_Controller_q, pla_1_out;
  wire [19:0] undriven;
  wire [31:0] multiplexer_2_out, multiplexer_3_out, V_Addr;

  Multiplexer #(.enable("true"), .width(32)) multiplexer_1 (
    .in0(MEM_Addr), .in1(IF_Addr), .out({V_Addr[31:22], TLB_Write[11:2], V_Addr[11:0]}), .sel(IF_REQ),
    .en(REQ));
  and and_1 (En_MMU_t, REQ, En_MMU);
  and and_2 (and_2_out, ~Hit, En_MMU_t);  // AND_Gate
  and and_3 (and_3_out, En_MMU_t, ~Hit, ~IF_REQ);  // AND_Gate
  Counter #(.max('h2), .width(2)) Page_Controller (
    .count(and_2_out), .Q(Page_Controller_q), .clk(Clk), .clr(RST));  // open: load, D, carry, up
  Multiplexer #(.width(32)) multiplexer_2 (.in0(Data_In), .in1(multiplexer_3_out), .out(multiplexer_2_out), .sel(Hit));
  Multiplexer #(.width(32)) multiplexer_3 (.in0(d_TLB), .in1(i_TLB), .out(multiplexer_3_out), .sel(IF_REQ));
  PLA #(.\table ("01 01 # PTE\n10 10 # Addr\n11 10 # NOP")) pla_1 (.in(Mux), .out(pla_1_out));
  Demultiplexer demultiplexer_1 (.out0(Write_d_TLB), .out1(Write_i_TLB), .in(pla_1_out[0]), .sel(IF_REQ));
  and and_4 (and_4_out, ~pla_1_out[1], and_3_out);  // AND_Gate
  Multiplexer #(.select(2), .width(32)) multiplexer_4 (
    .in0({CR3[31:12], V_Addr[31:22], 2'b00}), .in1({TLB_Write[31:2], 2'b00}), .in2({undriven, V_Addr[11:0]}),
    .in3({V_Addr[31:22], TLB_Write[11:2], V_Addr[11:0]}), .out(Addr), .sel(Mux));
  Multiplexer #(.width(2)) multiplexer_5 (.in0(2'b11), .in1(multiplexer_6_out), .out(Mux), .sel(En_MMU_t));
  Multiplexer #(.width(2)) multiplexer_6 (.in0(Page_Controller_q), .in1(2'b10), .out(multiplexer_6_out), .sel(Hit));
  and and_5 (IF_Write, IF_REQ, pla_1_out[1]);
  or or_1 (STALL, and_4_out, Stall_RAM);

  assign TLB_Write[1:0] = 2'b00;

  // Other names for the same wires on the sheet: V_Addr[21:12] = TLB_Write[11:2]

  // Notes on the sheet:
  //   CONTROLLER
endmodule

module Fault_Generator (
  input  [31:0] Datra_In
);
endmodule

module MMU_Registers (
  input  [3:0] E,
  input  [31:0] Data_In,
  input  Clk,
  input  RST,
  input  [3:0] W,
  input  En_RegE,
  input  [31:0] CR2_In,
  output [31:0] Data_Out,
  output [31:0] PCID_Out,
  output [31:0] CR3_Out,
  output [31:0] CR0_Out
);

  wire decoder_1_out3, decoder_1_out4, decoder_1_out6;
  wire [31:0] CR2_q, pull_resistor_1_node;

  Decoder #(.select(3)) decoder_1 (
    .out3(decoder_1_out3), .out4(decoder_1_out4), .out6(decoder_1_out6), .sel(W[2:0]), .en(En_RegE));  // open: out0, out1, out2, out5, out7
  Register #(.width(32)) PCID (.D(Data_In), .en(decoder_1_out3), .clk(Clk), .Q(PCID_Out), .clr(RST));
  Register #(.width(32)) CR3 (.D(Data_In), .en(decoder_1_out4), .clk(Clk), .Q(CR3_Out), .clr(RST));
  Register #(.width(32)) CR2 (.D(CR2_In), .clk(Clk), .Q(CR2_q), .clr(RST));  // open: en
  Register #(.width(32)) CR0 (.D(Data_In), .en(decoder_1_out6), .clk(Clk), .Q(CR0_Out), .clr(RST));
  Pull_Resistor pull_resistor_1 (.node(pull_resistor_1_node));
  Multiplexer #(.select(3), .width(32)) multiplexer_1 (
    .in0(pull_resistor_1_node), .in1(pull_resistor_1_node), .in2(pull_resistor_1_node), .in3(PCID_Out),
    .in4(CR3_Out), .in5(CR2_q), .in6(CR0_Out), .in7(pull_resistor_1_node), .out(Data_Out), .sel(E[2:0]));

  // Other names for the same wires on the sheet: Sel[2:0] = W[2:0]
endmodule

// VHDL entity TLB_LRU, as the project stores it:
-- =============================================================================
--  TLB_LRU.vhd
--  Translation Lookaside Buffer de 32 bits con reemplazo LRU
--  Optimizado para simulación en Logisim / GHDL
-- =============================================================================
--  ARQUITECTURA:
--    · Lookup COMBINACIONAL (asíncrono): responde sin esperar el clock,
--      ideal para simulación en Logisim.
--    · Escritura y actualización de edad LRU SÍNCRONA (flanco de subida).
--    · 64 entradas. Cada entrada guarda:
--        valid  (1 bit)
--        vpn    (20 bits, virt_addr[31:12])
--        pcid_k (8 bits,  pcid[7:0])
--        frame  (32 bits)
--        age    (6 bits, 0 = LRU, 63 = MRU)
--
--  POLÍTICA LRU (orden relativo siempre preservado):
--    · En HIT  → sea A = age[hit_idx] ANTES de promover.
--                age[hit_idx] = MAX
--                age[i]-- SOLO si age[i] > A   ← clave: no tocar entradas
--                                                  ya más viejas que hit
--    · En WRITE → sea A = age[víctima] ANTES de reemplazar.
--                 se inserta con age = MAX
--                 age[i]-- SOLO si valid[i] AND age[i] > A
--    · Prioridad: write_en > lookup hit (si ambas llegan al mismo ciclo)
--
--  ¿Por qué? Si decrementaras TODAS las entradas en cada hit, después de
--  suficientes hits en la misma entrada todas las demás llegarían a 0 y
--  perderías el orden relativo entre ellas (empate masivo en LRU).
-- =============================================================================

library IEEE;
use IEEE.STD_LOGIC_1164.ALL;
use IEEE.NUMERIC_STD.ALL;

entity TLB_LRU is
    Generic (
        -- Parámetros: 64 entradas (puedes ajustar)
        NUM_ENTRIES   : integer := 64;  -- 64 entradas en la TLB

        -- Reducimos la comparación a VPN y PCID pequeño (más realista)
        VPN_HIGH      : integer := 31;
        VPN_LOW       : integer := 12;  -- página de 4 KB → 20 bits de VPN
        PCID_LOW_BITS : integer := 7    -- usamos 8 bits de PCID (bits 7..0)
    );
    Port (
        clk           : in  STD_LOGIC;
        reset         : in  STD_LOGIC;

        -- Búsqueda (ASÍNCRONA combinacional para simulación / Logisim)
        lookup_en     : in  STD_LOGIC;                      -- Habilitar búsqueda
        pcid          : in  STD_LOGIC_VECTOR(31 downto 0);  -- Process-Context ID
        virt_addr     : in  STD_LOGIC_VECTOR(31 downto 0);  -- Dirección virtual (32 bits)
        hit           : out STD_LOGIC;                      -- '1' si encontró
        phys_frame    : out STD_LOGIC_VECTOR(31 downto 0);  -- Marco físico (32 bits)

        -- Escritura (SÍNCRONA con reemplazo LRU automático)
        write_en      : in  STD_LOGIC;                      -- Habilitar escritura
        write_phys    : in  STD_LOGIC_VECTOR(31 downto 0)   -- Marco físico a insertar
    );
end TLB_LRU;

architecture Behavioral of TLB_LRU is

    -- -------------------------------------------------------------------------
    -- Constantes derivadas
    -- -------------------------------------------------------------------------
    constant VPN_BITS  : integer := VPN_HIGH - VPN_LOW + 1;  -- 20
    constant PCID_BITS : integer := PCID_LOW_BITS + 1;        -- 8  (bits 7..0)
    constant AGE_BITS  : integer := 4;                        -- log2(64) = 6
    constant MAX_AGE   : integer := NUM_ENTRIES - 1;          -- 63

    -- -------------------------------------------------------------------------
    -- Tipos de arrays para la tabla TLB
    -- -------------------------------------------------------------------------
    type t_vpn   is array(0 to NUM_ENTRIES-1) of std_logic_vector(VPN_BITS-1  downto 0);
    type t_pcid  is array(0 to NUM_ENTRIES-1) of std_logic_vector(PCID_BITS-1 downto 0);
    type t_frame is array(0 to NUM_ENTRIES-1) of std_logic_vector(31 downto 0);
    type t_age   is array(0 to NUM_ENTRIES-1) of unsigned(AGE_BITS-1 downto 0);
    type t_valid is array(0 to NUM_ENTRIES-1) of std_logic;

    -- -------------------------------------------------------------------------
    -- Registros de la TLB
    -- -------------------------------------------------------------------------
    signal tlb_valid : t_valid;
    signal tlb_vpn   : t_vpn;
    signal tlb_pcid  : t_pcid;
    signal tlb_frame : t_frame;
    signal tlb_age   : t_age;

    -- -------------------------------------------------------------------------
    -- Señales de resultado del bloque combinacional
    -- (leídas por el bloque síncrono para actualizar la edad en HIT)
    -- -------------------------------------------------------------------------
    signal s_hit_found : std_logic;
    signal s_hit_idx   : integer range 0 to NUM_ENTRIES-1;

begin

    -- =========================================================================
    -- BLOQUE 1: Lookup combinacional (asíncrono)
    -- =========================================================================
    -- Responde en el mismo ciclo de simulación sin esperar un flanco de clock.
    -- Recorre todas las entradas en paralelo (síntesis) o en delta-cycles
    -- (simulación) y devuelve hit + phys_frame.
    -- También actualiza las señales internas s_hit_found / s_hit_idx que
    -- serán leídas por el bloque síncrono para el aging LRU en hit.
    -- =========================================================================
    comb_lookup : process(lookup_en, virt_addr, pcid,
                          tlb_valid, tlb_vpn, tlb_pcid, tlb_frame)
        variable v_vpn   : std_logic_vector(VPN_BITS-1  downto 0);
        variable v_pcid  : std_logic_vector(PCID_BITS-1 downto 0);
        variable v_found : std_logic;
        variable v_frame : std_logic_vector(31 downto 0);
        variable v_idx   : integer range 0 to NUM_ENTRIES-1;
    begin
        -- Extraer campos de comparación
        v_vpn  := virt_addr(VPN_HIGH downto VPN_LOW);
        v_pcid := pcid(PCID_LOW_BITS downto 0);

        -- Valores por defecto (miss)
        v_found := '0';
        v_frame := (others => '0');
        v_idx   := 0;

        -- Recorrido de las 64 entradas (en síntesis: lógica paralela)
        if lookup_en = '1' then
            for i in 0 to NUM_ENTRIES-1 loop
                if tlb_valid(i) = '1'
                   and tlb_vpn(i)  = v_vpn
                   and (tlb_pcid(i) = v_pcid or tlb_frame(i)(3) = '1')
                then
                    v_found := '1';
                    v_frame := tlb_frame(i);
                    v_idx   := i;
                    -- No hay break en VHDL; si hubiera dos hits (no debería)
                    -- el último índice gana. En una TLB correcta no hay duplicados.
                end if;
            end loop;
        end if;

        -- Salidas principales
        hit        <= v_found;
        phys_frame <= v_frame;

        -- Señales internas para el bloque síncrono
        s_hit_found <= v_found;
        s_hit_idx   <= v_idx;
    end process comb_lookup;


    -- =========================================================================
    -- BLOQUE 2: Actualización síncrona de la TLB y política LRU
    -- =========================================================================
    -- En cada flanco de subida de clk:
    --   · reset  → invalida todo
    --   · write_en = '1' → inserta nueva entrada con LRU replacement
    --   · write_en = '0' y hit = '1' → promueve la entrada a MRU
    -- Prioridad: write_en > hit (si llegan juntos, se procesa la escritura).
    -- =========================================================================
    sync_tlb : process(clk)
        variable v_vpn        : std_logic_vector(VPN_BITS-1  downto 0);
        variable v_pcid_w     : std_logic_vector(PCID_BITS-1 downto 0);
        variable v_target     : integer range 0 to NUM_ENTRIES-1;
        variable v_lru_idx    : integer range 0 to NUM_ENTRIES-1;
        variable v_min_age    : unsigned(AGE_BITS-1 downto 0);
        variable v_free_found : boolean;
        variable v_free_idx   : integer range 0 to NUM_ENTRIES-1;
        -- Captura la edad de la víctima/hit ANTES de sobreescribirla,
        -- necesaria para el decremento selectivo correcto.
        variable v_victim_age : unsigned(AGE_BITS-1 downto 0);
    begin
        if rising_edge(clk) then

            -- -----------------------------------------------------------------
            -- Reset: invalida toda la tabla y pone las edades a 0
            -- -----------------------------------------------------------------
            if reset = '1' then
                for i in 0 to NUM_ENTRIES-1 loop
                    tlb_valid(i) <= '0';
                    tlb_age(i)   <= (others => '0');
                end loop;

            -- -----------------------------------------------------------------
            -- Escritura con reemplazo LRU
            -- -----------------------------------------------------------------
            elsif write_en = '1' then
                v_vpn    := virt_addr(VPN_HIGH downto VPN_LOW);
                v_pcid_w := pcid(PCID_LOW_BITS downto 0);

                -- Paso 1: Buscar entrada libre (inválida) o la de menor edad
                v_free_found := false;
                v_free_idx   := 0;
                v_min_age    := (others => '1');  -- inicializar al máximo
                v_lru_idx    := 0;

                for i in 0 to NUM_ENTRIES-1 loop
                    -- Primera entrada inválida encontrada = candidata gratis
                    if tlb_valid(i) = '0' and not v_free_found then
                        v_free_found := true;
                        v_free_idx   := i;
                    end if;
                    -- Mínima edad (LRU real)
                    if tlb_age(i) < v_min_age then
                        v_min_age := tlb_age(i);
                        v_lru_idx := i;
                    end if;
                end loop;

                -- Paso 2: Elegir víctima y capturar su edad actual
                if v_free_found then
                    v_target     := v_free_idx;
                    v_victim_age := tlb_age(v_free_idx); -- 0 si era inválida
                else
                    v_target     := v_lru_idx;
                    v_victim_age := v_min_age;            -- edad LRU real
                end if;

                -- Paso 3: Insertar la nueva entrada como MRU
                tlb_vpn(v_target)   <= v_vpn;
                tlb_pcid(v_target)  <= v_pcid_w;
                tlb_frame(v_target) <= write_phys;
                tlb_valid(v_target) <= '1';
                tlb_age(v_target)   <= to_unsigned(MAX_AGE, AGE_BITS);

                -- Paso 4: Decrementar SOLO las entradas más recientes que la víctima.
                --   Invariante: si age[i] <= v_victim_age, esas entradas ya eran
                --   más viejas que la víctima y no deben cambiar su posición relativa.
                for i in 0 to NUM_ENTRIES-1 loop
                    if i /= v_target then
                        if tlb_valid(i) = '1' and tlb_age(i) > v_victim_age then
                            tlb_age(i) <= tlb_age(i) - 1;
                        end if;
                    end if;
                end loop;

            -- -----------------------------------------------------------------
            -- Hit: promover la entrada encontrada a MRU.
            -- CORRECCIÓN LRU: solo decrementan las entradas cuya edad sea
            -- MAYOR que la edad actual de la entrada en hit.  Las entradas
            -- que ya eran más viejas que hit conservan su posición relativa.
            -- -----------------------------------------------------------------
            elsif lookup_en = '1' and s_hit_found = '1' then
                -- Capturar la edad actual del hit (antes de promoverla)
                v_victim_age := tlb_age(s_hit_idx);

                for i in 0 to NUM_ENTRIES-1 loop
                    if i = s_hit_idx then
                        -- Entrada accedida → MRU
                        tlb_age(i) <= to_unsigned(MAX_AGE, AGE_BITS);
                    elsif tlb_valid(i) = '1' and tlb_age(i) > v_victim_age then
                        -- Solo las entradas más recientes que hit pierden un puesto
                        tlb_age(i) <= tlb_age(i) - 1;
                        -- Las entradas con age <= v_victim_age ya eran más viejas
                        -- que hit: su orden relativo entre sí no debe cambiar.
                    end if;
                end loop;
            end if;

        end if;
    end process sync_tlb;

end Behavioral;

-- =============================================================================
-- NOTAS DE USO
-- =============================================================================
--
--  1. LOOKUP (asíncrono):
--       · Pon lookup_en = '1', virt_addr y pcid en los pines.
--       · hit y phys_frame responden sin esperar el clock.
--       · La actualización LRU del hit se efectúa en el siguiente flanco.
--
--  2. ESCRITURA (síncrona):
--       · Pon write_en = '1', virt_addr, pcid y write_phys en los pines.
--       · La inserción y el reemplazo LRU ocurren en el flanco de subida.
--       · write_en tiene prioridad sobre lookup_en si llegan juntos.
--
--  3. RESET:
--       · reset = '1' (síncrono) invalida todas las entradas en el
--         siguiente flanco de subida.
--
--  4. AJUSTE DE TAMAÑO:
--       · Para una TLB más pequeña (y más rápida en Logisim) baja
--         NUM_ENTRIES a 16 o 32.
--       · Ajusta AGE_BITS = ceil(log2(NUM_ENTRIES)):
--           16 entradas → AGE_BITS = 4
--           32 entradas → AGE_BITS = 5
--           64 entradas → AGE_BITS = 6  (valor actual)
--
--  5. LOGISIM:
--       · Compila con GHDL y exporta el netlist.
--       · El loop de 64 entradas genera lógica paralela; si el simulador
--         va lento, reduce NUM_ENTRIES a 16 y ajusta AGE_BITS.
-- =============================================================================
