// Logisim project Unidad_Aritmetica.circ as structural Verilog: 2 circuits, main circuit ALU
module ALU (
  input  [31:0] A,
  input  [3:0] Op,
  input  [31:0] B,
  output [31:0] RES,
  output Carry,
  output [31:0] Over_Out
);

  wire adder_1_cout, and_2_out, not_1_out, pla_1_out, subtractor_1_bout;
  wire [4:0] bit_extender_1_out, bit_extender_2_out;
  wire [31:0] adder_1_out, and_1_out, demultiplexer_1_out0, demultiplexer_1_out1, demultiplexer_1_out2,
       demultiplexer_1_out3, demultiplexer_1_out4, demultiplexer_1_out5, demultiplexer_1_out6,
       demultiplexer_1_out7, demultiplexer_1_out8, demultiplexer_2_out0, demultiplexer_2_out1,
       demultiplexer_2_out2, demultiplexer_2_out3, demultiplexer_2_out4, demultiplexer_2_out5,
       demultiplexer_2_out6, demultiplexer_2_out7, demultiplexer_2_out8, divider_1_out, divider_1_rem,
       multiplier_1_cout, multiplier_1_out, nor_1_out, shifter_1_out, shifter_2_out, subtractor_1_out,
       xor_1_out;

  Demultiplexer #(.select(4), .width(32)) demultiplexer_1 (
    .out0(demultiplexer_1_out0), .out1(demultiplexer_1_out1), .out2(demultiplexer_1_out2),
    .out3(demultiplexer_1_out3), .out4(demultiplexer_1_out4), .out5(demultiplexer_1_out5),
    .out6(demultiplexer_1_out6), .out7(demultiplexer_1_out7), .out8(demultiplexer_1_out8), .in(A), .sel(Op));  // open: out9, out10, out11, out12, out13, out14, out15
  Demultiplexer #(.select(4), .width(32)) demultiplexer_2 (
    .out0(demultiplexer_2_out0), .out1(demultiplexer_2_out1), .out2(demultiplexer_2_out2),
    .out3(demultiplexer_2_out3), .out4(demultiplexer_2_out4), .out5(demultiplexer_2_out5),
    .out6(demultiplexer_2_out6), .out7(demultiplexer_2_out7), .out8(demultiplexer_2_out8), .in(B), .sel(Op));  // open: out9, out10, out11, out12, out13, out14, out15
  Adder #(.width(32)) adder_1 (
    .a(demultiplexer_1_out0), .b(demultiplexer_2_out0), .out(adder_1_out), .cout(adder_1_cout));  // open: cin
  Subtractor #(.width(32)) subtractor_1 (
    .a(demultiplexer_1_out1), .b(demultiplexer_2_out1), .out(subtractor_1_out), .bout(subtractor_1_bout));  // open: bin
  not not_1 (not_1_out, subtractor_1_bout);
  Multiplier #(.width(32)) multiplier_1 (
    .a(demultiplexer_1_out2), .b(demultiplexer_2_out2), .out(multiplier_1_out), .cout(multiplier_1_cout));  // open: cin
  Divider #(.width(32)) divider_1 (
    .a(demultiplexer_1_out3), .b(demultiplexer_2_out3), .out(divider_1_out), .rem(divider_1_rem));  // open: upper
  assign nor_1_out = ~(demultiplexer_1_out4 | demultiplexer_2_out4);  // NOR_Gate nor_1, 32 bits wide
  assign and_1_out = demultiplexer_1_out5 & demultiplexer_2_out5;  // AND_Gate and_1, 32 bits wide
  assign xor_1_out = demultiplexer_1_out6 ^ demultiplexer_2_out6;  // XOR_Gate xor_1, 32 bits wide
  Shifter #(.shift("lr"), .width(32)) shifter_1 (
    .in(demultiplexer_1_out7), .\dist (bit_extender_1_out), .out(shifter_1_out));
  Bit_Extender #(.in_width(32), .out_width(5), .\type ("zero")) bit_extender_1 (
    .in(demultiplexer_2_out7), .out(bit_extender_1_out));
  Shifter #(.width(32)) shifter_2 (.in(demultiplexer_1_out8), .\dist (bit_extender_2_out), .out(shifter_2_out));
  Bit_Extender #(.in_width(32), .out_width(5), .\type ("zero")) bit_extender_2 (
    .in(demultiplexer_2_out8), .out(bit_extender_2_out));
  Multiplexer #(.select(4), .width(32)) multiplexer_1 (
    .in0(adder_1_out), .in1(subtractor_1_out), .in2(multiplier_1_out), .in3(divider_1_out), .in4(nor_1_out),
    .in5(and_1_out), .in6(xor_1_out), .in7(shifter_1_out), .in8(shifter_2_out), .out(RES), .sel(Op));  // open: in9, in10, in11, in12, in13, in14, in15
  PLA #(.in_width(4), .out_width(1), .\table ("0001 1 # SUB")) pla_1 (.in(Op), .out(pla_1_out));
  assign Over_Out = multiplier_1_cout | divider_1_rem;  // OR_Gate or_1, 32 bits wide
  and and_2 (and_2_out, pla_1_out, not_1_out);
  or or_2 (Carry, and_2_out, adder_1_cout);
endmodule

module Branch (
  input  [31:0] RES,
  input  Carry,
  input  [31:0] A,
  input  [31:0] B,
  input  [31:0] Overflow,
  input  En,
  input  Clk,
  input  [3:0] Sel,
  input  [31:0] Data_Flags,
  input  [3:0] W,
  input  REGE_En,
  output Branch_Out,
  output [31:0] Carry_Out
);

  wire and_1_out, and_2_out, or_3_out, or_4_out;
  wire [1:0] plarom_1_p3;
  wire [2:0] bit_extender_1_out;
  wire [7:0] bit_extender_3_out, comparator_1_eq, multiplexer_1_out, register_1_q;
  wire [31:0] bit_extender_2_out, multiplexer_2_out, or_1_out;

  Bit_Extender #(.in_width(4), .out_width(3), .\type ("zero")) bit_extender_1 (.in(Sel), .out(bit_extender_1_out));
  // PlaRom #(.Contents("2 1 1 2 2 1 2 1 0 1 1 0"), .Select("high"), .\and (2), .outputs(2)) plarom_1: pin names not known; wires that end beside it: W, REGE_En, plarom_1_p3
  assign bit_extender_2_out = {{31{1'b0}}, Carry};  // Bit_Extender bit_extender_2
  Pull_Resistor pull_resistor_1 (.node(plarom_1_p3));
  and and_1 (and_1_out, ~A[31], ~B[31], RES[31]);  // AND_Gate
  and and_2 (and_2_out, A[31], B[31], ~RES[31]);  // AND_Gate
  assign or_1_out = bit_extender_2_out | Overflow;  // OR_Gate or_1, 32 bits wide
  Comparator #(.mode("unsigned"), .width(32)) comparator_1 (
    .a(RES), .b({32{1'b0}}), .eq(comparator_1_eq[0]));  // open: gt, lt
  or or_2 (comparator_1_eq[6], and_1_out, and_2_out);
  not not_1 (comparator_1_eq[1], comparator_1_eq[0]);
  not not_2 (comparator_1_eq[3], RES[31]);
  not not_3 (comparator_1_eq[5], Carry);
  not not_4 (comparator_1_eq[7], comparator_1_eq[6]);
  Multiplexer #(.width(8)) multiplexer_1 (
    .in0({comparator_1_eq[7:5], Carry, comparator_1_eq[3], RES[31], comparator_1_eq[1:0]}),
    .in1(bit_extender_3_out), .out(multiplexer_1_out), .sel(plarom_1_p3[0]));
  Bit_Extender #(.in_width(32), .out_width(8), .\type ("zero")) bit_extender_3 (
    .in(Data_Flags), .out(bit_extender_3_out));
  or or_3 (or_3_out, plarom_1_p3[0], En);
  Multiplexer #(.width(32)) multiplexer_2 (
    .in0(or_1_out), .in1(Data_Flags), .out(multiplexer_2_out), .sel(plarom_1_p3[1]));
  Register register_1 (.D(multiplexer_1_out), .en(or_3_out), .Q(register_1_q), .clk(Clk));  // open: clr
  or or_4 (or_4_out, En, plarom_1_p3[1]);
  Multiplexer #(.select(3)) multiplexer_3 (
    .in0(register_1_q[0]), .in1(register_1_q[1]), .in2(register_1_q[2]), .in3(register_1_q[3]),
    .in4(register_1_q[4]), .in5(register_1_q[5]), .in6(register_1_q[6]), .in7(register_1_q[7]),
    .out(Branch_Out), .sel(bit_extender_1_out));
  Register #(.width(32)) register_2 (.D(multiplexer_2_out), .en(or_4_out), .Q(Carry_Out), .clk(Clk));  // open: clr

  // Notes on the sheet:
  //   Zero
endmodule
