// Logisim project TTY_Controller.circ as structural Verilog: 3 circuits, main circuit TTY_Main
module TTY_Main (
  input  [6:0] Ctrl_Down,
  input  [63:0] Data_In,
  input  [31:0] Addr_In,
  output [31:0] Addr_To_RAM,
  output [1:0] Ctrl_Up,
  output [63:0] Data_Out,
  output Clk,
  output En_Write,
  output Clear,
  output [6:0] Data
);

  wire IRQ, msi_sys_1_bus_req, msi_sys_1_msi, or_1_out, tlp_receptor_1_dma_ack, tlp_receptor_1_ecam,
       tlp_receptor_1_en_read_cpu, tlp_receptor_1_en_write_cpu, tlp_receptor_1_mmio, tlp_receptor_1_rst,
       tty_controller_1_bus_req, tty_controller_1_clean_regs;
  wire [15:0] endpoint_ecam_1_comand, M_Config, tty_controller_1_status;
  wire [31:0] endpoint_ecam_1_bar_out_0, endpoint_ecam_1_data_out, MA, MD, msi_sys_1_addr,
       msi_sys_1_data_out, multiplexer_2_out, multiplexer_3_out, registers_bar0_tty_1_cant_out,
       registers_bar0_tty_1_comand_out, registers_bar0_tty_1_data_out, registers_bar0_tty_1_w_a,
       tty_controller_1_addr_to_ram;

  TLP_Receptor tlp_receptor_1 (
    .Bus_REQ(or_1_out), .En_Write(msi_sys_1_msi), .Ctrl_Downstream(Ctrl_Down), .ECAM(tlp_receptor_1_ecam),
    .MMIO(tlp_receptor_1_mmio), .En_Write_CPU(tlp_receptor_1_en_write_cpu),
    .En_Read_CPU(tlp_receptor_1_en_read_cpu), .DMA_ACK(tlp_receptor_1_dma_ack), .Clk(Clk),
    .RST(tlp_receptor_1_rst), .Ctrl_Upstream(Ctrl_Up));
  EndPoint_ECAM endpoint_ecam_1 (
    .Write(tlp_receptor_1_en_write_cpu), .RST(tlp_receptor_1_rst), .Clk(Clk), .Data_In(Data_In),
    .Addr(Addr_In), .Is_ECAM(tlp_receptor_1_ecam), .Read(tlp_receptor_1_en_read_cpu),
    .Status(tty_controller_1_status), .Vendor_Device(32'h7a320003), .Class_Code(24'h70000),
    .Header_Type({8{1'b0}}), .ERBA({32{1'b1}}), .In_BAR_0(32'hc), .In_BAR_1({32{1'b0}}),
    .In_BAR_2({32{1'b0}}), .In_BAR_3({32{1'b0}}), .Next_Pointer({8{1'b1}}), .MSI_Cant(3'b000),
    .BAR_Out_0(endpoint_ecam_1_bar_out_0), .Data_Out(endpoint_ecam_1_data_out),
    .Comand(endpoint_ecam_1_comand), .M_Config(M_Config), .MA(MA), .MD(MD));  // open: BAR_Out_1, BAR_Out_2, BAR_Out_3
  Multiplexer #(.width(32)) multiplexer_1 (
    .in0(tty_controller_1_addr_to_ram), .in1(msi_sys_1_addr), .out(Addr_To_RAM), .sel(msi_sys_1_msi));
  Registers_BAR0_TTY registers_bar0_tty_1 (
    .BAR_0(endpoint_ecam_1_bar_out_0), .BAR_0_REQ(32'hc), .MMIO(tlp_receptor_1_mmio),
    .Ctrl(endpoint_ecam_1_comand), .Clean_Reg(tty_controller_1_clean_regs), .RST(tlp_receptor_1_rst),
    .Clk(Clk), .Read(tlp_receptor_1_en_read_cpu), .Write(tlp_receptor_1_en_write_cpu), .Data_In(Data_In),
    .Addr(Addr_In), .Data_Out(registers_bar0_tty_1_data_out), .Comand_Out(registers_bar0_tty_1_comand_out),
    .W_A(registers_bar0_tty_1_w_a), .Cant_Out(registers_bar0_tty_1_cant_out));
  Multiplexer #(.enable("true"), .width(32)) multiplexer_2 (
    .in0(endpoint_ecam_1_data_out), .in1(registers_bar0_tty_1_data_out), .out(multiplexer_2_out),
    .sel(tlp_receptor_1_mmio), .en(tlp_receptor_1_en_read_cpu));
  or or_1 (or_1_out, msi_sys_1_bus_req, tty_controller_1_bus_req);
  TTY_Controller tty_controller_1 (
    .Comand(registers_bar0_tty_1_comand_out), .W_A(registers_bar0_tty_1_w_a), .Clk(Clk),
    .DMA_ACK(tlp_receptor_1_dma_ack), .RST(tlp_receptor_1_rst), .Cant(registers_bar0_tty_1_cant_out),
    .Ctrl(endpoint_ecam_1_comand), .Data_From_RAM(Data_In), .Status(tty_controller_1_status),
    .Addr_To_RAM(tty_controller_1_addr_to_ram), .Data_Out(Data), .IRQ(IRQ), .Write_En(En_Write),
    .Clear(Clear), .Bus_REQ(tty_controller_1_bus_req), .Clean_Regs(tty_controller_1_clean_regs));
  assign Data_Out = {{32{1'b0}}, multiplexer_3_out};  // Bit_Extender bit_extender_1
  Multiplexer #(.width(32)) multiplexer_3 (
    .in0(multiplexer_2_out), .in1(msi_sys_1_data_out), .out(multiplexer_3_out), .sel(msi_sys_1_msi));
  MSI_Sys msi_sys_1 (
    .M_config(M_Config), .Code({5{1'b0}}), .MD(MD), .IRQ(IRQ), .CLK(Clk), .MA(MA),
    .DMA_ACK(tlp_receptor_1_dma_ack), .Addr(msi_sys_1_addr), .MSI(msi_sys_1_msi),
    .Bus_REQ(msi_sys_1_bus_req), .Data_Out(msi_sys_1_data_out));
endmodule

module TTY_Controller (
  input  [15:0] Ctrl,
  input  [31:0] Comand,
  input  RST,
  input  [31:0] W_A,
  input  [31:0] Cant,
  input  Clk,
  input  DMA_ACK,
  input  [63:0] Data_From_RAM,
  output [15:0] Status,
  output Clean_Regs,
  output Write_En,
  output Clear,
  output Bus_REQ,
  output [31:0] Addr_To_RAM,
  output [6:0] Data_Out,
  output IRQ
);

  wire and_1_out, and_2_out, and_3_out, and_4_out, and_6_out, and_7_out, and_8_out, and_9_out, and_10_out,
       and_11_out, and_12_out, and_13_out, and_14_out, and_15_out, and_16_out, and_17_out, and_18_out,
       and_21_out, Busy, comparator_1_eq, comparator_2_eq, comparator_3_eq, counter_1_carry, counter_3_carry,
       d_ff_1_q, d_ff_2_qn, DMA, Error, Final_Detected, Finish, Full, No_IRQ, not_1_out, or_2_out, or_3_out,
       or_4_out, or_6_out, or_7_out, or_8_out, RST_t, Starting, Valid, Write_A;
  wire [1:0] Data_Sel_out, Status_Dec_out;
  wire [2:0] bit_extender_1_out, counter_2_q, counter_3_q, multiplexer_1_out, register_1_q;
  wire [2:1] DMA_Dec_out;
  wire [3:1] Main_out;
  wire [6:0] bit_extender_2_out, bit_extender_3_out;
  wire [7:0] CHAR, multiplexer_6_out;
  wire [31:0] adder_1_out, counter_1_q, multiplexer_2_out;
  wire [63:0] Char_Buffer_p5, Char_Buffer_p6, Char_Buffer_p7, Char_Buffer_p8, Char_Buffer_p9,
       Char_Buffer_p10, Char_Buffer_p11, Char_Buffer_p12, multiplexer_4_out;

  Bit_Extender #(.in_width(32), .out_width(3), .\type ("zero")) bit_extender_1 (.in(Comand), .out(bit_extender_1_out));
  and and_1 (and_1_out, Starting, ~Busy);  // AND_Gate
  or or_1 (RST_t, RST, Error, Finish);
  Adder #(.width(32)) adder_1 (.a(Addr_To_RAM), .b(32'h8), .out(adder_1_out));  // open: cin, cout
  and and_2 (and_2_out, Starting, ~Busy);  // AND_Gate
  and and_3 (and_3_out, Valid, Write_A, Starting, ~Clear);  // AND_Gate
  and and_4 (and_4_out, ~Clear, Starting, ~Valid, ~Write_A);  // AND_Gate
  and and_5 (DMA, DMA_ACK, Bus_REQ);
  PLA #(.in_width(5), .out_width(1), .\table ("10001 1 # Write A")) DMA_Dec (
    .in({multiplexer_1_out, Ctrl[1:0]}), .out(DMA_Dec_out[1]));
  Multiplexer #(.width(3)) multiplexer_1 (
    .in0(bit_extender_1_out), .in1(register_1_q), .out(multiplexer_1_out), .sel(Busy));
  Register #(.width(3)) register_1 (.D(bit_extender_1_out), .en(and_1_out), .Q(register_1_q), .clk(Clk), .clr(RST_t));
  Multiplexer #(.width(32)) multiplexer_2 (.in0(W_A), .in1(adder_1_out), .out(multiplexer_2_out), .sel(Busy));
  or or_2 (or_2_out, and_2_out, DMA, and_3_out);
  or or_3 (or_3_out, and_3_out, and_4_out);
  and and_6 (and_6_out, DMA, Busy, Valid, Write_A);
  and and_7 (and_7_out, Busy, DMA, Write_A);
  PLA #(.in_width(5), .out_width(1), .\table ("001x1 1 # Write\n010x1 1 # Delete\n011x1 1 # Clear\n100x1 1 # Write A\n000x1 1 # NOP\nxxxx0 1 # OFF")) State (
    .in({multiplexer_1_out, Ctrl[1:0]}), .out(DMA_Dec_out[2]));
  PLA #(.in_width(5), .out_width(5), .\table ("001x1 00011 # Write\n010x1 00101 # Delete\n011x1 01001 # Clear\n10011 10001 # Write A")) Main (
    .in({multiplexer_1_out, Ctrl[1:0]}), .out({Write_A, Main_out, Starting}));
  Register #(.width(32)) register_2 (.D(multiplexer_2_out), .en(or_2_out), .Q(Addr_To_RAM), .clk(Clk), .clr(RST_t));
  Counter #(.max('hffffffff), .width(32)) counter_1 (
    .load(and_2_out), .D(Cant), .count(or_3_out), .Q(counter_1_q), .carry(counter_1_carry), .up(and_2_out),
    .clk(Clk), .clr(RST_t));
  and and_8 (and_8_out, DMA, or_8_out);
  not not_1 (not_1_out, counter_3_carry);
  or or_4 (or_4_out, and_6_out, counter_3_carry);
  // Shift_Register #(.width(64)) Char_Buffer: pin names not known; wires that end beside it: RST_t, and_7_out, Clk, Data_From_RAM, Char_Buffer_p5, Char_Buffer_p6, Char_Buffer_p7, Char_Buffer_p8, Char_Buffer_p9, Char_Buffer_p10, Char_Buffer_p11, Char_Buffer_p12
  PLA #(.in_width(3), .out_width(3), .\table ("100 000 # Ready\n101 001 # Busy\n0xx 110 # Innvalid\n11x 111 # Not DMA")) Status_Dec (
    .in({DMA_Dec_out, Busy}), .out({Error, Status_Dec_out}));
  or or_5 (No_IRQ, Main_out[2], Main_out[1]);
  PLA #(.in_width(5), .\table ("00011 00 # Write\n00101 01 # Delete\n10001 10 # Write A")) Data_Sel (
    .in({Write_A, Main_out, Starting}), .out(Data_Sel_out));
  Bit_Extender #(.in_width(32), .out_width(7), .\type ("zero")) bit_extender_2 (
    .in(Addr_To_RAM), .out(bit_extender_2_out));
  Bit_Extender #(.out_width(7), .\type ("zero")) bit_extender_3 (.in(CHAR), .out(bit_extender_3_out));
  Comparator #(.mode("unsigned"), .width(32)) comparator_1 (
    .a(32'h1), .b(counter_1_q), .eq(comparator_1_eq));  // open: gt, lt
  and and_9 (and_9_out, Write_En, ~Write_A, counter_1_carry);  // AND_Gate
  Counter #(.max('h7), .width(3)) counter_2 (
    .count(and_10_out), .Q(counter_2_q), .carry(Full), .up(not_1_out), .clk(Clk), .clr(RST_t));  // open: load, D
  and and_10 (and_10_out, or_4_out, ~and_8_out);  // AND_Gate
  assign Status = {{14{1'b0}}, Status_Dec_out};  // Bit_Extender bit_extender_4
  and and_11 (and_11_out, ~Clear, Busy);  // AND_Gate
  and and_12 (and_12_out, ~and_11_out, Starting);  // AND_Gate
  or or_6 (or_6_out, Main_out[1], Main_out[2], Write_A);
  Multiplexer #(.enable("true"), .select(2), .width(7)) multiplexer_3 (
    .in0(bit_extender_2_out), .in1(7'b0001000), .in2(bit_extender_3_out), .out(Data_Out), .sel(Data_Sel_out),
    .en(Write_En));  // open: in3
  or or_7 (or_7_out, Clear, and_13_out);
  and and_13 (and_13_out, No_IRQ, ~Write_A, comparator_1_eq);  // AND_Gate
  or or_8 (or_8_out, Full, comparator_2_eq);
  T_Flip_Flop t_ff_1 (.T(and_12_out), .clk(Clk), .Q(Busy), .reset(RST_t));  // open: Qn, preset
  D_Flip_Flop d_ff_1 (.D(and_14_out), .clk(Clk), .Q(d_ff_1_q));  // open: Qn, preset, reset
  and and_14 (and_14_out, Busy, ~or_7_out);  // AND_Gate
  S_R_Flip_Flop s_r_ff_1 (.S(DMA), .clk(Clk), .R(1'b0), .Q(Valid), .reset(RST_t));  // open: Qn, preset
  and and_15 (and_15_out, Main_out[3], Busy);
  Counter #(.max('h7), .width(3)) counter_3 (
    .count(Valid), .Q(counter_3_q), .carry(counter_3_carry), .clk(Clk), .clr(RST_t));  // open: load, D, up
  Multiplexer #(.select(3), .width(64)) multiplexer_4 (
    .in0(Char_Buffer_p5), .in1(Char_Buffer_p6), .in2(Char_Buffer_p7), .in3(Char_Buffer_p8),
    .in4(Char_Buffer_p9), .in5(Char_Buffer_p10), .in6(Char_Buffer_p11), .in7(Char_Buffer_p12),
    .out(multiplexer_4_out), .sel(counter_2_q));
  and and_16 (and_16_out, d_ff_2_qn, Starting, ~Busy);  // AND_Gate
  and and_17 (and_17_out, Valid, Write_A, Busy, or_6_out);
  and and_18 (and_18_out, or_6_out, Busy, ~Write_A);  // AND_Gate
  and and_19 (Bus_REQ, Write_A, ~Full, ~Final_Detected, Busy);  // AND_Gate
  and and_20 (IRQ, d_ff_1_q, ~and_14_out);  // AND_Gate
  or or_9 (Finish, IRQ, Final_Detected, and_9_out);
  Comparator #(.mode("unsigned"), .width(3)) comparator_2 (
    .a(3'b111), .b(counter_3_q), .eq(comparator_2_eq));  // open: gt, lt
  Multiplexer #(.select(3), .width(8)) multiplexer_5 (
    .in0(multiplexer_4_out[7:0]), .in1(multiplexer_4_out[15:8]), .in2(multiplexer_4_out[23:16]),
    .in3(multiplexer_4_out[31:24]), .in4(multiplexer_4_out[39:32]), .in5(multiplexer_4_out[47:40]),
    .in6(multiplexer_4_out[55:48]), .in7(multiplexer_4_out[63:56]), .out(CHAR), .sel(counter_3_q));
  D_Flip_Flop d_ff_2 (.D(and_16_out), .clk(Clk), .Q(Clean_Regs), .Qn(d_ff_2_qn), .reset(RST_t));  // open: preset
  or or_10 (Write_En, and_17_out, and_18_out);
  or or_11 (Clear, and_15_out, RST);
  Comparator #(.mode("unsigned")) comparator_3 (
    .a({8{1'b0}}), .b(multiplexer_6_out), .eq(comparator_3_eq));  // open: gt, lt
  Multiplexer #(.width(8)) multiplexer_6 (.in0({8{1'b1}}), .in1(CHAR), .out(multiplexer_6_out), .sel(Valid));
  T_Flip_Flop t_ff_2 (.T(and_21_out), .clk(Clk), .Q(Final_Detected), .reset(RST_t));  // open: Qn, preset
  and and_21 (and_21_out, Write_A, Valid, comparator_3_eq);

  // Other names for the same wires on the sheet: Write = Write_En

  // Notes on the sheet:
  //   Controler
  //   Main Counter
  //   Buffer
  //   Finish Detector
endmodule

module Registers_BAR0_TTY (
  input  [31:0] Addr,
  input  Clean_Reg,
  input  RST,
  input  Clk,
  input  Read,
  input  Write,
  input  [63:0] Data_In,
  input  MMIO,
  input  [15:0] Ctrl,
  input  [31:0] BAR_0,
  input  [31:0] BAR_0_REQ,
  output [31:0] Data_Out,
  output [31:0] Comand_Out,
  output [31:0] W_A,
  output [31:0] Cant_Out
);

  wire and_1_out, and_2_out, and_3_out, and_5_out, comparator_1_eq, comparator_1_gt, comparator_2_eq,
       comparator_2_gt, decoder_1_out0, decoder_1_out1, decoder_1_out2, Enable, or_1_out, or_2_out, or_3_out;
  wire [31:0] adder_1_out, bit_extender_1_out;

  Adder #(.width(32)) adder_1 (.a(BAR_0), .b(BAR_0_REQ), .out(adder_1_out));  // open: cin, cout
  or or_1 (or_1_out, Clean_Reg, RST);
  and and_1 (and_1_out, Read, Enable);
  and and_2 (and_2_out, Enable, Write);
  Bit_Extender #(.in_width(64), .out_width(32), .\type ("zero")) bit_extender_1 (
    .in(Data_In), .out(bit_extender_1_out));
  Decoder #(.select(2)) decoder_1 (
    .out0(decoder_1_out0), .out1(decoder_1_out1), .out2(decoder_1_out2), .sel(Addr[3:2]), .en(and_2_out));  // open: out3
  and and_3 (and_3_out, MMIO, Ctrl[0]);
  or or_2 (or_2_out, comparator_1_gt, comparator_1_eq);
  Comparator #(.mode("unsigned"), .width(32)) comparator_1 (
    .a(Addr), .b(BAR_0), .gt(comparator_1_gt), .eq(comparator_1_eq));  // open: lt
  or or_3 (or_3_out, comparator_2_gt, comparator_2_eq);
  Comparator #(.mode("unsigned"), .width(32)) comparator_2 (
    .a(adder_1_out), .b(Addr), .gt(comparator_2_gt), .eq(comparator_2_eq));  // open: lt
  and and_4 (Enable, and_3_out, and_5_out);
  and and_5 (and_5_out, or_2_out, or_3_out);
  Register #(.width(32)) Comand (
    .D(bit_extender_1_out), .en(decoder_1_out0), .clk(Clk), .Q(Comand_Out), .clr(or_1_out));
  Register #(.width(32)) Word_Addr (.D(bit_extender_1_out), .en(decoder_1_out1), .clk(Clk), .Q(W_A), .clr(or_1_out));
  Register #(.width(32)) Cant (.D(bit_extender_1_out), .en(decoder_1_out2), .clk(Clk), .Q(Cant_Out), .clr(or_1_out));
  Multiplexer #(.enable("true"), .select(2), .width(32)) multiplexer_1 (
    .in0(Comand_Out), .in1(W_A), .in2(Cant_Out), .out(Data_Out), .sel(Addr[3:2]), .en(and_1_out));  // open: in3
endmodule
