// Logisim project Main_Memories.circ as structural Verilog: 2 circuits, main circuit Memory
module Memory (
  input  [31:0] Addr,
  input  RST,
  input  Read_En,
  input  [7:0] Write_Flags,
  input  Clk,
  input  [31:0] Data_In,
  input  Write_En,
  output RAM_Ready,
  output [63:0] out_9
);

  wire decoder_1_out0, decoder_1_out1, decoder_1_out2, decoder_1_out3;
  wire [7:0] ram_1_p5, ram_1_p6, ram_1_p7, ram_1_p8, ram_1_p9, ram_1_p10, ram_1_p11, ram_1_p12, ram_2_p5,
       ram_3_p5, ram_3_p6, ram_3_p7, ram_3_p8, ram_3_p9, ram_3_p10, ram_3_p11, ram_3_p12, ram_4_p5, ram_4_p6,
       ram_4_p7, ram_4_p8, ram_4_p9, ram_4_p10, ram_4_p11, ram_4_p12, undriven, undriven_2, undriven_3,
       undriven_4, undriven_5, undriven_6, undriven_7;

  Decoder #(.select(2)) decoder_1 (
    .out0(decoder_1_out0), .out1(decoder_1_out1), .out2(decoder_1_out2), .out3(decoder_1_out3),
    .sel(Addr[31:30]), .en(Write_En));
  // RAM #(.addrWidth(30), .clearpin("true"), .enables("line"), .line("octo"), .misaligned("true")) ram_1: pin names not known; wires that end beside it: Addr[29:0], decoder_1_out3, Clk, RST, ram_1_p5, ram_1_p6, ram_1_p7, ram_1_p8, ram_1_p9, ram_1_p10, ram_1_p11, ram_1_p12
  // RAM #(.addrWidth(30), .clearpin("true"), .enables("line"), .line("octo"), .misaligned("true")) ram_2: pin names not known; wires that end beside it: Addr[29:0], decoder_1_out0, Clk, RST, ram_2_p5
  // RAM #(.addrWidth(30), .clearpin("true"), .enables("line"), .line("octo"), .misaligned("true")) ram_3: pin names not known; wires that end beside it: Addr[29:0], decoder_1_out1, Clk, RST, ram_3_p5, ram_3_p6, ram_3_p7, ram_3_p8, ram_3_p9, ram_3_p10, ram_3_p11, ram_3_p12
  // RAM #(.addrWidth(30), .clearpin("true"), .enables("line"), .line("octo"), .misaligned("true")) ram_4: pin names not known; wires that end beside it: Addr[29:0], decoder_1_out2, Clk, RST, ram_4_p5, ram_4_p6, ram_4_p7, ram_4_p8, ram_4_p9, ram_4_p10, ram_4_p11, ram_4_p12
  Multiplexer #(.enable("true"), .select(2), .width(64)) multiplexer_1 (
    .in0({ram_3_p11, ram_3_p10, ram_3_p9, ram_3_p8, ram_3_p7, ram_3_p6, ram_3_p5, ram_2_p5}),
    .in1({ram_4_p11, ram_4_p10, ram_4_p9, ram_4_p8, ram_4_p7, ram_4_p6, ram_4_p5, ram_3_p12}),
    .in2({undriven_7, undriven_6, undriven_5, undriven_4, undriven_3, undriven_2, undriven, ram_4_p12}),
    .in3({ram_1_p12, ram_1_p11, ram_1_p10, ram_1_p9, ram_1_p8, ram_1_p7, ram_1_p6, ram_1_p5}), .out(out_9),
    .sel(Addr[31:30]), .en(Read_En));

  assign RAM_Ready = 1'b1;

  // Other names for the same wires on the sheet: Sel[1:0] = Addr[31:30]
endmodule

module ROM_BIOS (
  input  [19:0] Addr,
  output [63:0] Data_Out
);

  // ROM #(.addrWidth(20), .line("octo"), .misaligned("true")) rom_1: pin names not known; wires that end beside it: Addr, Data_Out[31:24], Data_Out[23:16], Data_Out[15:8], Data_Out[7:0], Data_Out[63:56], Data_Out[55:48], Data_Out[47:40], Data_Out[39:32]

  // Notes on the sheet:
  //   contents of rom_1 (hex, n*v repeats v):
  //   d e0 0 38 53 e8 0 14 53 e9 0 10 53 ea 0 c 53 eb 0 8 53 ec 0 4 53 ed 0 0 53 e4 0 28 c 40 0 ff 53 e1 0
  //   1c 3 41 0 0 8c f0 ff f0 8d f0 0 44 f 4f 0 0 8c f0 ff f0 8d f0 0 64 e f 0 0 52 ed 0 0 52 ec 0 4 52 eb
  //   0 8 52 ea 0 c 52 e9 0 10 52 e8 0 14 d e0 ff c8 11 0 0 0 c 10 0 14 52 e4 0 1c a 41 10 0 6 11 10 0 c
  //   60 0 0 8c 60 e0 0 8d 60 0 0 6 66 60 0 6 16 10 0 53 e1 0 34 c d0 0 0 c 80 ff ff c b0 0 0 8c b0 c0 0
  //   8d b0 0 0 c c0 0 8 53 ed 0 20 53 e2 0 24 53 e3 0 2c 53 e5 0 30 52 e6 0 34 82 d0 90 0 52 61 0 0 7 18
  //   10 0 3 18 0 0 8c f0 ff f0 8d f0 6 80 f f 0 0 8c f0 ff f0 8d f0 0 e0 e f 0 0 52 31 0 0 c 70 0 3f 3 71
  //   0 0 8c f0 ff f0 8d f0 0 44 f 2f 0 0 8c f0 ff f0 8d f0 1 4 e f 0 0 c 70 0 13 4 17 10 0 2 21 70 0 52
  //   51 0 0 2 1b 10 0 c d0 0 18 9 1d a0 0 13 7a 0 3 c 40 0 10 9 14 a0 0 13 7a 0 2 13 71 0 0 9 1c 10 0 13
  //   71 0 1 52 eb 0 1c 13 7b 0 10 52 e1 0 20 13 71 0 11 53 e9 0 18 13 79 0 12 52 61 0 8 9 1d a0 0 13 7a 0
  //   f 9 14 a0 0 13 7a 0 e 13 71 0 c 9 1c 10 0 13 71 0 d 52 61 0 8 9 1d 10 0 c 90 0 7f 7 19 10 0 c a0 0 1
  //   3 1a 0 0 8c f0 ff f0 8d f0 4 3c f f 0 0 8c f0 ff f0 8d f0 1 a4 e f 0 0 c b0 0 0 8c b0 c0 0 8d b0 0 0
  //   c d0 0 0 3 1d 0 0 8c f0 ff f0 8d f0 7 2c f 1f 0 0 8c f0 ff f0 8d f0 1 d0 e f 0 0 c 20 0 0 8c 20 0 0
  //   8d 20 ff ff 53 62 10 0 52 61 10 0 c 80 0 18 82 80 90 0 3 1d 0 0 8c f0 ff f0 8d f0 2 4c f f 0 0 8c f0
  //   ff f0 8d f0 2 8 e f 0 0 52 5a 0 0 2 ab a0 0 53 6a 10 0 c 80 10 0 82 80 a0 0 3 81 0 0 8c f0 ff f0 8d
  //   f0 2 2c f 4f 0 0 d 10 f ff c a0 0 0 8c a0 0 0 8d a0 f0 0 7 1a a0 0 52 51 0 0 2 1a 10 0 53 51 0 0 53
  //   62 10 4 52 61 10 4 3 1d 0 0 8c f0 ff f0 8d f0 2 b4 f f 0 0 8c f0 ff f0 8d f0 2 70 e f 0 0 52 5a 0 0
  //   2 ab a0 0 53 6a 10 4 c 80 10 0 82 80 a0 0 3 81 0 0 8c f0 ff f0 8d f0 2 94 f 4f 0 0 d 10 f ff c a0 0
  //   0 8c a0 0 0 8d a0 f0 0 7 1a a0 0 52 51 0 0 2 1a 10 0 53 51 0 0 53 62 10 8 52 61 10 8 3 1d 0 0 8c f0
  //   ff f0 8d f0 3 1c f f 0 0 8c f0 ff f0 8d f0 2 d8 e f 0 0 52 5a 0 0 2 ab a0 0 53 6a 10 8 c 80 10 0 82
  //   80 a0 0 3 81 0 0 8c f0 ff f0 8d f0 2 fc f 4f 0 0 d 10 f ff c a0 0 0 8c a0 0 0 8d a0 f0 0 7 1a a0 0
  //   52 51 0 0 2 1a 10 0 53 51 0 0 53 62 10 c 52 61 10 c 3 1d 0 0 8c f0 ff f0 8d f0 3 40 f 1f 0 0 8c f0
  //   ff f0 8d f0 6 f0 e f 0 0 52 5a 0 0 2 ab a0 0 53 6a 10 c c 20 10 1 3 12 0 0 8c f0 ff f0 8d f0 3 6c f
  //   4f 0 0 8c f0 ff f0 8d f0 7 0 e f 0 0 52 51 0 0 d 10 10 0 53 51 0 0 12 7a 0 2 a a4 a0 0 6 aa a0 0 12
  //   7b 0 3 a b9 b0 0 6 bb b0 0 6 ba a0 0 12 7b 0 1 a bc b0 0 6 bb b0 0 82 90 c0 0 12 78 0 0 6 88 80 0 6
  //   b8 80 0 6 aa a0 0 6 88 80 0 6 a8 80 0 3 18 10 0 c b0 0 0 8c b0 c0 0 8d b0 0 0 2 1b 10 0 9 14 80 0 13
  //   78 0 a 9 1c 80 0 13 78 0 b 13 71 0 8 c 20 0 8 9 12 10 0 13 71 0 9 52 51 0 0 2 1b 10 0 9 1c 80 0 c c0
  //   0 8 13 78 0 7 9 14 80 0 13 78 0 6 13 71 0 4 9 1c 10 0 13 71 0 5 52 31 0 0 d 10 0 1 53 31 0 0 c 80 ff
  //   ff 52 e2 0 24 52 e9 0 18 8c f0 ff f0 8d f0 6 80 e f 0 0 52 31 0 0 d 10 0 1 53 31 0 0 82 c0 90 0 c c0
  //   0 10 52 e4 0 28 52 41 0 0 52 68 10 0 c a0 0 0 8c a0 ff 0 8d a0 0 0 7 8a 80 0 6 88 80 0 a 1c a0 0 c
  //   d0 0 0 8c d0 0 ff 8d d0 0 0 7 ad a0 0 6 aa a0 0 6 a8 80 0 6 bb a0 0 6 88 80 0 6 8a 80 0 53 68 10 0 c
  //   80 0 ff 7 18 10 0 52 48 0 0 d 80 0 1 53 48 0 0 8c f0 ff f0 8d f0 0 0 10 f 0 0 52 68 10 0 c 20 0 0 8c
  //   20 ff 0 8d 20 0 ff 7 82 80 0 a 19 10 0 6 11 10 0 6 88 80 0 6 81 10 0 52 48 0 0 82 c0 30 0 a 83 80 0
  //   2 8d 80 0 7 8d 80 0 6 11 10 0 6 88 80 0 6 81 10 0 53 61 10 0 52 51 0 0 c 20 0 0 8c 20 c0 0 8d 20 0 0
  //   2 12 a0 0 c 20 0 18 9 a2 80 0 13 78 0 7 9 a3 80 0 13 78 0 6 9 a9 80 0 13 78 0 5 13 7a 0 4 12 78 0 2
  //   a 83 80 0 6 88 80 0 12 7b 0 3 a b2 b0 0 6 bb b0 0 6 b8 80 0 12 7b 0 1 a b9 b0 0 6 bb b0 0 12 7d 0 0
  //   6 dd d0 0 6 bd b0 0 6 88 80 0 6 bb b0 0 6 8b 80 0 3 a8 80 0 9 82 b0 0 13 7b 0 b 9 83 b0 0 13 7b 0 a
  //   13 78 0 8 9 89 80 0 13 78 0 9 12 78 0 1 12 78 0 0 12 78 0 2 12 7b 0 3 12 7d 0 2 a d3 d0 0 6 dd d0 0
  //   12 7c 0 3 a c2 c0 0 6 cc c0 0 6 cd c0 0 12 7d 0 1 a d9 d0 0 6 dd d0 0 12 77 0 0 6 77 70 0 6 d7 70 0
  //   6 cc c0 0 6 77 70 0 6 c7 c0 0 a b2 70 0 a 83 80 0 6 88 80 0 6 77 70 0 6 78 70 0 9 73 70 0 82 70 b0 0
  //   3 ca 0 0 8c f0 ff f0 8d f0 6 14 f 4f 0 0 c 20 0 0 8c 20 c0 0 8d 20 ff ff 2 12 10 0 c 20 0 1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
endmodule
