// Logisim project ECAMs.circ as structural Verilog
module ECAM_Mapper (
  input  [31:0] Addr,
  output Is_ECAM,
  output [11:0] Reg_sel,
  output [2:0] Func,
  output [4:0] Disp,
  output [5:0] Bus_Dir
);

  Comparator #(.mode("unsigned"), .width(6)) comparator_1 (
    .a(Addr[31:26]), .b(6'b111000), .eq(Is_ECAM));  // open: gt, lt

  assign Bus_Dir = Addr[25:20];
  assign Disp = Addr[19:15];
  assign Func = Addr[14:12];
  assign Reg_sel = Addr[11:0];

  // Notes on the sheet:
  //   ECAM=E00 a E3F
endmodule

module Port_ECAM (
  input  Read,
  input  Is_ECAM,
  input  RST,
  input  Clk,
  input  [31:0] Data_In,
  input  [11:0] Addr,
  input  [15:0] Status,
  input  [31:0] Vendor_Device,
  input  [23:0] Class_Code,
  input  [7:0] Header_Type,
  input  [11:0] Capabilities_Pointer,
  output [31:0] Data_Out,
  output [15:0] Comand,
  output [31:0] PSS0_Out,
  output [31:0] Base_Limit
);

  wire and_3_out, and_4_out, and_5_out, comparator_2_eq, comparator_2_gt, CP, decoder_1_out0, decoder_1_out2,
       Not_Common, Read_t;
  wire [2:0] and_2_out, pla_2_out;
  wire [3:0] bit_extender_2_out, pla_1_out;
  wire [31:0] bit_extender_1_out, common_ecam_1_data_out, multiplexer_1_out;

  and and_1 (Read_t, Read, Is_ECAM);
  Comparator #(.mode("unsigned"), .width(12)) comparator_1 (.a(12'h10), .b(Addr), .gt(and_2_out[1]));  // open: eq, lt
  Comparator #(.mode("unsigned"), .width(12)) comparator_2 (
    .a(Addr), .b(Capabilities_Pointer), .gt(comparator_2_gt), .eq(comparator_2_eq));  // open: lt
  assign bit_extender_1_out = {{20{1'b0}}, Capabilities_Pointer};  // Bit_Extender bit_extender_1
  and and_2 (and_2_out[0], Is_ECAM, ~Read_t);  // AND_Gate
  or or_1 (and_2_out[2], comparator_2_gt, comparator_2_eq);
  PLA #(.in_width(3), .out_width(4), .\table ("010 0000 # Com\n000 1001 # NCom\n100 0110 # CP")) pla_1 (
    .in(and_2_out), .out(pla_1_out));
  PLA #(.in_width(3), .out_width(3), .\table ("xx0 000 # NOT\n001 010 # NCom\n011 100 # Com\n101 001 # CP")) pla_2 (
    .in(and_2_out), .out(pla_2_out));
  and and_3 (and_3_out, ~Read_t, Not_Common);  // AND_Gate
  Decoder #(.select(2)) decoder_1 (
    .out0(decoder_1_out0), .out2(decoder_1_out2), .sel(Addr[3:2]), .en(and_3_out));  // open: out1, out3
  Bit_Extender #(.in_width(12), .out_width(4), .\type ("zero")) bit_extender_2 (.in(Addr), .out(bit_extender_2_out));
  Register #(.width(32)) PSS0 (.D(Data_In), .en(decoder_1_out0), .clk(Clk), .Q(PSS0_Out), .clr(RST));
  Register #(.width(32)) MBase_MLimit (.D(Data_In), .en(decoder_1_out2), .clk(Clk), .Q(Base_Limit), .clr(RST));
  and and_4 (and_4_out, pla_1_out[3], Read_t);
  and and_5 (and_5_out, Read_t, pla_1_out[2]);
  or or_2 (CP, and_5_out, pla_2_out[0]);
  or or_3 (Not_Common, and_4_out, pla_2_out[1]);
  Common_ECAM common_ecam_1 (
    .Clk(Clk), .RST(RST), .Data_In(Data_In), .Addr(bit_extender_2_out), .Is_Common_ECAM(pla_2_out[2]),
    .Vendor_Device(Vendor_Device), .Status(Status), .Class_Code(Class_Code), .Header_Type(Header_Type),
    .Comand_Out(Comand), .Data_Out(common_ecam_1_data_out));
  Multiplexer #(.enable("true"), .select(2), .width(32)) multiplexer_1 (
    .in0(PSS0_Out), .in1(bit_extender_1_out), .in2(Base_Limit), .out(multiplexer_1_out), .sel(Addr[3:2]),
    .en(Not_Common));  // open: in3
  Multiplexer #(.enable("true"), .select(2), .width(32)) multiplexer_2 (
    .in0(common_ecam_1_data_out), .in1(multiplexer_1_out), .out(Data_Out), .sel(pla_1_out[1:0]), .en(Read_t));  // open: in2, in3
endmodule

module EndPoint_ECAM (
  input  Write,
  input  [31:0] Addr
);

  Comparator #(.mode("unsigned"), .width(6)) comparator_1 (.a(Addr[31:26]), .b(6'b111000));  // open: gt, eq, lt
  Common_ECAM common_ecam_1 ();  // open: Clk, RST, Data_In, Addr, Is_Common_ECAM, Vendor_Device, Status, Class_Code, Header_Type, Comand_Out, Data_Out
endmodule

module Common_ECAM (
  input  [3:0] Addr,
  input  Is_Common_ECAM,
  input  Clk,
  input  RST,
  input  [31:0] Data_In,
  input  [31:0] Vendor_Device,
  input  [15:0] Status,
  input  [23:0] Class_Code,
  input  [7:0] Header_Type,
  output [15:0] Comand_Out,
  output [31:0] Data_Out
);

  wire decoder_1_out1;
  wire [15:0] bit_extender_1_out;

  Decoder #(.select(2)) decoder_1 (
    .out1(decoder_1_out1), .sel(Addr[3:2]), .en(Is_Common_ECAM));  // open: out0, out2, out3
  Bit_Extender #(.in_width(32), .\type ("zero")) bit_extender_1 (.in(Data_In), .out(bit_extender_1_out));
  Register #(.width(16)) Command (.D(bit_extender_1_out), .en(decoder_1_out1), .clk(Clk), .Q(Comand_Out), .clr(RST));
  Multiplexer #(.select(2), .width(32)) multiplexer_1 (
    .in0(Vendor_Device), .in1({Status, Comand_Out}), .in2({Header_Type, Class_Code}), .out(Data_Out),
    .sel(Addr[3:2]));  // open: in3
endmodule
