// Logisim project mother.circ as structural Verilog: 2 circuits, main circuit main
module main (
);

  wire button_1_out, clock_1_out, die_1_p1, die_1_p10, die_1_p12, die_1_p13, die_1_p15, die_1_p16, die_1_p21,
       die_1_p22, die_1_p23, die_1_p24, die_1_p25, die_1_p26, die_1_p27, die_1_p28, die_1_p29, die_1_p30,
       die_1_p31, die_1_p32, keyboard_main_1_p7, keyboard_main_1_p8, keyboard_main_1_p9, keyboard_main_1_p10,
       on_off_sys_1_clk_out, on_off_sys_1_rst_out, tty_main_1_p8, tty_main_1_p9, tty_main_1_p10;
  wire [1:0] minirouter_1_out_12, nvm_main_1_ctrl_up;
  wire [6:0] die_1_p6, keyboard_main_1_p11, minirouter_1_ctrl_down_1, tty_main_1_p7;
  wire [7:0] die_1_p11;
  wire [19:0] die_1_p14;
  wire [31:0] die_1_p4, die_1_p19, minirouter_1_addr_to_perif_1, minirouter_1_out_9, nvm_main_1_addr_to_ram;
  wire [63:0] die_1_p5, die_1_p18, die_1_p20, minirouter_1_data_to_perif_1, minirouter_1_out_10,
       nvm_main_1_data_out, rom_bios_1_data_out;

  LED led_1 (.in(die_1_p1));
  Clock #(.highDuration(275), .lowDuration(275)) clock_1 (.out(clock_1_out));
  Button button_1 (.out(button_1_out));
  On_Off_Sys on_off_sys_1 (
    .RST(button_1_out), .Clk(clock_1_out), .RST_Out(on_off_sys_1_rst_out), .Clk_Out(on_off_sys_1_clk_out));
  miniRouter minirouter_1 (
    .in_1(die_1_p5), .in_2(die_1_p4), .in_5(die_1_p6), .Addr_From_Perif_1(nvm_main_1_addr_to_ram),
    .Data_From_Perif_1(nvm_main_1_data_out), .Ctrl_Up_1(nvm_main_1_ctrl_up), .out_9(minirouter_1_out_9),
    .out_10(minirouter_1_out_10), .out_12(minirouter_1_out_12),
    .Data_To_Perif_1(minirouter_1_data_to_perif_1), .Addr_To_Perif_1(minirouter_1_addr_to_perif_1),
    .Ctrl_Down_1(minirouter_1_ctrl_down_1));
  ROM_BIOS rom_bios_1 (.Addr(die_1_p14), .Data_Out(rom_bios_1_data_out));
  // Probe on die_1_p20
  // Probe on die_1_p18
  // Probe on die_1_p19
  // Die die_1: pin names not known; wires that end beside it: die_1_p1, on_off_sys_1_clk_out, on_off_sys_1_rst_out, die_1_p4, die_1_p5, die_1_p6, minirouter_1_out_9, minirouter_1_out_10, minirouter_1_out_12, die_1_p10, die_1_p11, die_1_p12, die_1_p13, die_1_p14, die_1_p15, die_1_p16, rom_bios_1_data_out, die_1_p18, die_1_p19, die_1_p20, die_1_p21, die_1_p22, die_1_p23, die_1_p24, die_1_p25, die_1_p26, die_1_p27, die_1_p28, die_1_p29, die_1_p30, die_1_p31, die_1_p32
  Memory memory_1 (
    .Write_En(die_1_p10), .RST(die_1_p16), .Read_En(die_1_p12), .Write_Flags(die_1_p11), .Clk(die_1_p15),
    .Data_In(die_1_p20), .Addr(die_1_p19), .RAM_Ready(die_1_p13), .out_9(die_1_p18));
  NVM_Main nvm_main_1 (
    .Ctrl_Down(minirouter_1_ctrl_down_1), .Data_In(minirouter_1_data_to_perif_1),
    .Addr_In(minirouter_1_addr_to_perif_1), .Data_Out(nvm_main_1_data_out), .Ctrl_Up(nvm_main_1_ctrl_up),
    .Addr_To_RAM(nvm_main_1_addr_to_ram));
  TTY #(.cols(40), .rows(10)) tty_1 (
    .data(tty_main_1_p7), .clk(tty_main_1_p8), .we(tty_main_1_p9), .clr(tty_main_1_p10));
  // TTY_Main tty_main_1: pin names not known; wires that end beside it: die_1_p21, die_1_p22, die_1_p23, die_1_p24, die_1_p25, die_1_p26, tty_main_1_p7, tty_main_1_p8, tty_main_1_p9, tty_main_1_p10
  // Keyboard_Main keyboard_main_1: pin names not known; wires that end beside it: die_1_p27, die_1_p28, die_1_p29, die_1_p30, die_1_p31, die_1_p32, keyboard_main_1_p7, keyboard_main_1_p8, keyboard_main_1_p9, keyboard_main_1_p10, keyboard_main_1_p11
  Keyboard keyboard_1 (
    .clk(keyboard_main_1_p7), .re(keyboard_main_1_p8), .clr(keyboard_main_1_p9), .avail(keyboard_main_1_p10),
    .data(keyboard_main_1_p11));
endmodule

module On_Off_Sys (
  input  RST,
  input  Clk,
  output RST_Out,
  output Clk_Out
);

  wire and_1_out, and_2_out, and_3_out, and_4_out, and_5_out, and_6_out, and_7_out, and_8_out, and_9_out,
       and_10_out, and_11_out, and_12_out, and_13_out, or_1_out, or_2_out, or_3_out, or_4_out, Q0, Q1, Q2;

  and and_1 (and_1_out, ~Q1, RST);  // AND_Gate
  and and_2 (and_2_out, ~Q1, Q0);  // AND_Gate
  and and_3 (and_3_out, Q0, RST);
  and and_4 (and_4_out, ~Q0, Q2);  // AND_Gate
  and and_5 (and_5_out, ~Q2, Q0);  // AND_Gate
  and and_6 (and_6_out, Q1, ~Q0);  // AND_Gate
  and and_7 (and_7_out, Q1, RST);
  and and_8 (and_8_out, Q2, ~Q0);  // AND_Gate
  and and_9 (and_9_out, Q2, RST);
  and and_10 (and_10_out, Q1, ~Q0, RST);  // AND_Gate
  or or_1 (or_1_out, and_1_out, and_2_out, and_3_out, and_4_out);
  or or_2 (or_2_out, and_5_out, and_6_out, and_7_out);
  or or_3 (or_3_out, and_8_out, and_9_out, and_10_out);
  D_Flip_Flop d_ff_1 (.D(or_1_out), .clk(Clk), .Q(Q0));  // open: Qn, preset, reset
  D_Flip_Flop d_ff_2 (.D(or_2_out), .clk(Clk), .Q(Q1));  // open: Qn, preset, reset
  D_Flip_Flop d_ff_3 (.D(or_3_out), .clk(Clk), .Q(Q2));  // open: Qn, preset, reset
  and and_11 (and_11_out, Q2, Q1, ~Q0);  // AND_Gate
  and and_12 (and_12_out, ~Q2, ~Q1, Q0);  // AND_Gate
  or or_4 (or_4_out, Q0, Q1);
  or or_5 (RST_Out, and_11_out, and_12_out);
  and and_13 (and_13_out, ~Q2, or_4_out);  // AND_Gate
  and and_14 (Clk_Out, and_13_out, Clk);
endmodule
